// Logisim project TinyCPU.circ as structural Verilog: 29 circuits, main circuit TinyCPUMain
module TinyCPUMain (
  input  CLK,
  input  RESET,
  output [15:0] PRINT_VALUE,
  output PRINT_ADDRESS_VALID,
  output [15:0] PRINT_ADDRESS_VALUE,
  output PRINT_VALID,
  output ERROR_OVF,
  output ERROR_DIV0,
  output ERROR_ADDR,
  output ERROR_INV,
  output ERROR_ILL,
  output ERROR_INPUT,
  output PRINT_ENABLE,
  output PRINT_ADDRESS_ENABLE,
  output HALTED,
  output HALTED_WITH_ERROR
);

  wire ADDRESS_PATH_address_valid, ADDRESS_PATH_offset_carry, ADDRESS_RANGE_FBOX_active_address_out_of_range,
       DATAPATH_INSTANCE_negative, DATAPATH_INSTANCE_zero, DECODE_SIGNALS_acc_memory_request,
       DECODE_SIGNALS_acc_write_request, EFFECTIVE_ADDRESS_FBOX_address_out_of_range,
       EFFECTIVE_ADDRESS_FBOX_effective_offset_mode, EFFECTIVE_ADDRESS_FBOX_effective_register_mode,
       FETCH_DECODE_halt_error, FETCH_DECODE_jump_not_zero, GROUPED_DECODE_ADAPTER_add_adr,
       GROUPED_DECODE_ADAPTER_add_adr_reg, GROUPED_DECODE_ADAPTER_add_const,
       GROUPED_DECODE_ADAPTER_add_reg_off, GROUPED_DECODE_ADAPTER_and_adr,
       GROUPED_DECODE_ADAPTER_and_adr_reg, GROUPED_DECODE_ADAPTER_and_const,
       GROUPED_DECODE_ADAPTER_and_reg_off, GROUPED_DECODE_ADAPTER_clear_error,
       GROUPED_DECODE_ADAPTER_div_adr, GROUPED_DECODE_ADAPTER_div_adr_reg, GROUPED_DECODE_ADAPTER_div_const,
       GROUPED_DECODE_ADAPTER_div_reg_off, GROUPED_DECODE_ADAPTER_input, GROUPED_DECODE_ADAPTER_jump_adr,
       GROUPED_DECODE_ADAPTER_jump_error, GROUPED_DECODE_ADAPTER_jump_negative,
       GROUPED_DECODE_ADAPTER_jump_not_error, GROUPED_DECODE_ADAPTER_jump_not_zero,
       GROUPED_DECODE_ADAPTER_jump_zero, GROUPED_DECODE_ADAPTER_ld_reg_adr,
       GROUPED_DECODE_ADAPTER_ld_reg_const, GROUPED_DECODE_ADAPTER_load_adr,
       GROUPED_DECODE_ADAPTER_load_adr_reg, GROUPED_DECODE_ADAPTER_load_const,
       GROUPED_DECODE_ADAPTER_load_reg_off, GROUPED_DECODE_ADAPTER_mul_adr,
       GROUPED_DECODE_ADAPTER_mul_adr_reg, GROUPED_DECODE_ADAPTER_mul_const,
       GROUPED_DECODE_ADAPTER_mul_reg_off, GROUPED_DECODE_ADAPTER_not, GROUPED_DECODE_ADAPTER_or_adr,
       GROUPED_DECODE_ADAPTER_or_adr_reg, GROUPED_DECODE_ADAPTER_or_const, GROUPED_DECODE_ADAPTER_or_reg_off,
       GROUPED_DECODE_ADAPTER_set_addr, GROUPED_DECODE_ADAPTER_set_div0, GROUPED_DECODE_ADAPTER_set_ill,
       GROUPED_DECODE_ADAPTER_set_input, GROUPED_DECODE_ADAPTER_set_inv, GROUPED_DECODE_ADAPTER_set_ovf,
       GROUPED_DECODE_ADAPTER_store_adr, GROUPED_DECODE_ADAPTER_store_adr_reg,
       GROUPED_DECODE_ADAPTER_store_reg_off, GROUPED_DECODE_ADAPTER_sub_adr,
       GROUPED_DECODE_ADAPTER_sub_adr_reg, GROUPED_DECODE_ADAPTER_sub_const,
       GROUPED_DECODE_ADAPTER_sub_reg_off, GROUPED_DECODE_ADAPTER_xor_adr,
       GROUPED_DECODE_ADAPTER_xor_adr_reg, GROUPED_DECODE_ADAPTER_xor_const,
       GROUPED_DECODE_ADAPTER_xor_reg_off, INVERT_ZERO_FOR_JNZ_out, MEMORY_WRITE_REQUEST_out,
       OPERATIONS_INSTANCE_divide_by_zero, OPERATIONS_INSTANCE_invalid_operand, OPERATIONS_INSTANCE_overflow,
       OPERATIONS_INSTANCE_result_is_valid;
  wire [11:0] FETCH_DECODE_pc_out;
  wire [15:0] ACC_LOAD_DATA_SELECT_out, ADDRESS_PATH_address, ADDRESS_PATH_address_plus_offset,
       EFFECTIVE_ADDRESS_FBOX_effective_memory_address,
       EFFECTIVE_ADDRESS_FBOX_effective_register_selected_out, OPERATIONS_INSTANCE_result_value;
  wire [21:0] FETCH_DECODE_opcode;

  or MEMORY_WRITE_REQUEST (MEMORY_WRITE_REQUEST_out, GROUPED_DECODE_ADAPTER_store_adr, GROUPED_DECODE_ADAPTER_store_adr_reg, GROUPED_DECODE_ADAPTER_store_reg_off);
  FetchDecode FETCH_DECODE (
    .CLK(CLK), .RESET(RESET), .DEC_JUMP_NOT_ZERO(GROUPED_DECODE_ADAPTER_jump_not_zero),
    .NOT_ZERO(INVERT_ZERO_FOR_JNZ_out), .PROGRAM_LIMIT(16'h1), .DEC_HALT_ERROR(1'b1),
    .JUMP_NOT_ZERO(FETCH_DECODE_jump_not_zero), .HALT_ERROR(FETCH_DECODE_halt_error),
    .PC_OUT(FETCH_DECODE_pc_out), .OPCODE(FETCH_DECODE_opcode));
  Memory MEMORY_INSTANCE (
    .ADDRESS(EFFECTIVE_ADDRESS_FBOX_effective_memory_address), .WRITE_ENABLE(MEMORY_WRITE_REQUEST_out),
    .CLK(CLK), .VALID_IN(PRINT_VALID), .DATA_IN(PRINT_VALUE), .MEMORY_VALID(PRINT_ADDRESS_VALID),
    .MEMORY_DATA(PRINT_ADDRESS_VALUE));
  // Probe on FETCH_DECODE_jump_not_zero
  // Probe on FETCH_DECODE_halt_error
  // Probe on FETCH_DECODE_pc_out
  AddressPath ADDRESS_PATH (
    .ADDRESS_IN(16'h1), .AR_LOAD(DECODE_SIGNALS_acc_write_request), .OFFSET(16'h1), .VALID_IN(1'b1),
    .CLK(CLK), .ADDRESS_PATH_STARTUP_RESET(1'b1), .ADDRESS(ADDRESS_PATH_address),
    .ADDRESS_PLUS_OFFSET(ADDRESS_PATH_address_plus_offset), .OFFSET_CARRY(ADDRESS_PATH_offset_carry),
    .ADDRESS_VALID(ADDRESS_PATH_address_valid));
  DecodeSignals DECODE_SIGNALS (
    .Opcode(FETCH_DECODE_opcode[21:16]), .ACC_MEMORY_REQUEST(DECODE_SIGNALS_acc_memory_request),
    .ACC_WRITE_REQUEST(DECODE_SIGNALS_acc_write_request));
  ControlAdapterBlock GROUPED_DECODE_ADAPTER (
    .OPCODE(FETCH_DECODE_opcode[21:16]), .LOAD_CONST(GROUPED_DECODE_ADAPTER_load_const),
    .LOAD_ADR(GROUPED_DECODE_ADAPTER_load_adr), .LOAD_ADR_REG(GROUPED_DECODE_ADAPTER_load_adr_reg),
    .LOAD_REG_OFF(GROUPED_DECODE_ADAPTER_load_reg_off), .ADD_CONST(GROUPED_DECODE_ADAPTER_add_const),
    .ADD_ADR(GROUPED_DECODE_ADAPTER_add_adr), .ADD_ADR_REG(GROUPED_DECODE_ADAPTER_add_adr_reg),
    .ADD_REG_OFF(GROUPED_DECODE_ADAPTER_add_reg_off), .SUB_CONST(GROUPED_DECODE_ADAPTER_sub_const),
    .SUB_ADR(GROUPED_DECODE_ADAPTER_sub_adr), .SUB_ADR_REG(GROUPED_DECODE_ADAPTER_sub_adr_reg),
    .SUB_REG_OFF(GROUPED_DECODE_ADAPTER_sub_reg_off), .MUL_CONST(GROUPED_DECODE_ADAPTER_mul_const),
    .MUL_ADR(GROUPED_DECODE_ADAPTER_mul_adr), .MUL_ADR_REG(GROUPED_DECODE_ADAPTER_mul_adr_reg),
    .MUL_REG_OFF(GROUPED_DECODE_ADAPTER_mul_reg_off), .DIV_CONST(GROUPED_DECODE_ADAPTER_div_const),
    .DIV_ADR(GROUPED_DECODE_ADAPTER_div_adr), .DIV_ADR_REG(GROUPED_DECODE_ADAPTER_div_adr_reg),
    .DIV_REG_OFF(GROUPED_DECODE_ADAPTER_div_reg_off), .AND_CONST(GROUPED_DECODE_ADAPTER_and_const),
    .AND_ADR(GROUPED_DECODE_ADAPTER_and_adr), .AND_ADR_REG(GROUPED_DECODE_ADAPTER_and_adr_reg),
    .AND_REG_OFF(GROUPED_DECODE_ADAPTER_and_reg_off), .OR_CONST(GROUPED_DECODE_ADAPTER_or_const),
    .OR_ADR(GROUPED_DECODE_ADAPTER_or_adr), .OR_ADR_REG(GROUPED_DECODE_ADAPTER_or_adr_reg),
    .OR_REG_OFF(GROUPED_DECODE_ADAPTER_or_reg_off), .STORE_ADR(GROUPED_DECODE_ADAPTER_store_adr),
    .STORE_ADR_REG(GROUPED_DECODE_ADAPTER_store_adr_reg),
    .STORE_REG_OFF(GROUPED_DECODE_ADAPTER_store_reg_off), .LD_REG_CONST(GROUPED_DECODE_ADAPTER_ld_reg_const),
    .LD_REG_ADR(GROUPED_DECODE_ADAPTER_ld_reg_adr), .NOT(GROUPED_DECODE_ADAPTER_not),
    .JUMP_ADR(GROUPED_DECODE_ADAPTER_jump_adr), .JUMP_ZERO(GROUPED_DECODE_ADAPTER_jump_zero),
    .JUMP_NOT_ZERO(GROUPED_DECODE_ADAPTER_jump_not_zero),
    .JUMP_NEGATIVE(GROUPED_DECODE_ADAPTER_jump_negative), .JUMP_ERROR(GROUPED_DECODE_ADAPTER_jump_error),
    .JUMP_NOT_ERROR(GROUPED_DECODE_ADAPTER_jump_not_error), .CLEAR_ERROR(GROUPED_DECODE_ADAPTER_clear_error),
    .INPUT(GROUPED_DECODE_ADAPTER_input), .PRINT(PRINT_ENABLE), .PRINT_ADR(PRINT_ADDRESS_ENABLE),
    .HALT(HALTED), .HALT_ERROR(HALTED_WITH_ERROR), .SET_OVF(GROUPED_DECODE_ADAPTER_set_ovf),
    .SET_DIV0(GROUPED_DECODE_ADAPTER_set_div0), .SET_ADDR(GROUPED_DECODE_ADAPTER_set_addr),
    .SET_INV(GROUPED_DECODE_ADAPTER_set_inv), .SET_ILL(GROUPED_DECODE_ADAPTER_set_ill),
    .SET_INPUT(GROUPED_DECODE_ADAPTER_set_input), .XOR_CONST(GROUPED_DECODE_ADAPTER_xor_const),
    .XOR_ADR(GROUPED_DECODE_ADAPTER_xor_adr), .XOR_ADR_REG(GROUPED_DECODE_ADAPTER_xor_adr_reg),
    .XOR_REG_OFF(GROUPED_DECODE_ADAPTER_xor_reg_off));
  // Probe on GROUPED_DECODE_ADAPTER_ld_reg_const
  // Probe on GROUPED_DECODE_ADAPTER_ld_reg_adr
  // Probe on GROUPED_DECODE_ADAPTER_jump_adr
  // Probe on GROUPED_DECODE_ADAPTER_jump_zero
  // Probe on GROUPED_DECODE_ADAPTER_jump_negative
  // Probe on GROUPED_DECODE_ADAPTER_jump_error
  // Probe on GROUPED_DECODE_ADAPTER_jump_not_error
  // Probe on GROUPED_DECODE_ADAPTER_input
  // Probe on GROUPED_DECODE_ADAPTER_set_div0
  // Probe on GROUPED_DECODE_ADAPTER_set_addr
  // Probe on GROUPED_DECODE_ADAPTER_set_inv
  Datapath DATAPATH_INSTANCE (
    .DATA_IN(OPERATIONS_INSTANCE_result_value), .DATAPATH_STARTUP_RESET(1'b0),
    .ACC_LOAD(DECODE_SIGNALS_acc_write_request), .VALID_IN(OPERATIONS_INSTANCE_result_is_valid), .CLK(CLK),
    .ACC_OUT(PRINT_VALUE), .ZERO(DATAPATH_INSTANCE_zero), .NEGATIVE(DATAPATH_INSTANCE_negative),
    .ACC_VALID_OUT(PRINT_VALID));
  not INVERT_ZERO_FOR_JNZ (INVERT_ZERO_FOR_JNZ_out, DATAPATH_INSTANCE_zero);
  Multiplexer #(.width(16)) ACC_LOAD_DATA_SELECT (
    .in0(FETCH_DECODE_opcode[15:0]), .in1(PRINT_ADDRESS_VALUE), .out(ACC_LOAD_DATA_SELECT_out),
    .sel(DECODE_SIGNALS_acc_memory_request));
  ErrorFlags ERROR_FLAGS (
    .CLEAR_ERROR(GROUPED_DECODE_ADAPTER_clear_error), .CLK(CLK), .SET_OVF(GROUPED_DECODE_ADAPTER_set_ovf),
    .SET_DIV0(OPERATIONS_INSTANCE_divide_by_zero), .SET_ADDR(ADDRESS_RANGE_FBOX_active_address_out_of_range),
    .SET_INV(OPERATIONS_INSTANCE_invalid_operand), .SET_ILL(GROUPED_DECODE_ADAPTER_set_ill),
    .SET_INPUT(GROUPED_DECODE_ADAPTER_set_input), .OVF_OUT(ERROR_OVF), .DIV0_OUT(ERROR_DIV0),
    .ADDR_OUT(ERROR_ADDR), .INV_OUT(ERROR_INV), .ILL_OUT(ERROR_ILL), .INPUT_OUT(ERROR_INPUT));
  Operations OPERATIONS_INSTANCE (
    .ADD_CONST(GROUPED_DECODE_ADAPTER_add_const), .ADD_ADDRESS(GROUPED_DECODE_ADAPTER_add_adr),
    .ADD_ADDRESS_REGISTER(GROUPED_DECODE_ADAPTER_add_adr_reg),
    .ADD_ADDRESS_REGISTER_PLUS_OFFSET(GROUPED_DECODE_ADAPTER_add_reg_off), .ACC_VALUE(PRINT_VALUE),
    .MEMORY_VALUE(PRINT_ADDRESS_VALUE), .IMMEDIATE_VALUE(ACC_LOAD_DATA_SELECT_out),
    .MEMORY_VALID(PRINT_ADDRESS_VALID), .ACC_VALID(PRINT_VALID),
    .SUB_CONST(GROUPED_DECODE_ADAPTER_sub_const), .SUB_ADDRESS(GROUPED_DECODE_ADAPTER_sub_adr),
    .SUB_ADDRESS_REGISTER(GROUPED_DECODE_ADAPTER_sub_adr_reg),
    .SUB_ADDRESS_REGISTER_PLUS_OFFSET(GROUPED_DECODE_ADAPTER_sub_reg_off),
    .NOT_IS_ACTIVE(GROUPED_DECODE_ADAPTER_not), .MUL_CONST(GROUPED_DECODE_ADAPTER_mul_const),
    .MUL_ADDRESS(GROUPED_DECODE_ADAPTER_mul_adr), .MUL_ADDRESS_REGISTER(GROUPED_DECODE_ADAPTER_mul_adr_reg),
    .MUL_ADDRESS_REGISTER_PLUS_OFFSET(GROUPED_DECODE_ADAPTER_mul_reg_off),
    .DIV_CONST(GROUPED_DECODE_ADAPTER_div_const),
    .DIV_ADDRESS_REGISTER_PLUS_OFFSET(GROUPED_DECODE_ADAPTER_div_reg_off),
    .DIV_ADDRESS(GROUPED_DECODE_ADAPTER_div_adr), .DIV_ADDRESS_REGISTER(GROUPED_DECODE_ADAPTER_div_adr_reg),
    .AND_CONST(GROUPED_DECODE_ADAPTER_and_const),
    .AND_ADDRESS_REGISTER_PLUS_OFFSET(GROUPED_DECODE_ADAPTER_and_reg_off),
    .AND_ADDRESS(GROUPED_DECODE_ADAPTER_and_adr), .AND_ADDRESS_REGISTER(GROUPED_DECODE_ADAPTER_and_adr_reg),
    .OR_CONST(GROUPED_DECODE_ADAPTER_or_const),
    .OR_ADDRESS_REGISTER_PLUS_OFFSET(GROUPED_DECODE_ADAPTER_or_reg_off),
    .OR_ADDRESS(GROUPED_DECODE_ADAPTER_or_adr), .OR_ADDRESS_REGISTER(GROUPED_DECODE_ADAPTER_or_adr_reg),
    .XOR_CONST(GROUPED_DECODE_ADAPTER_xor_const),
    .XOR_ADDRESS_REGISTER_PLUS_OFFSET(GROUPED_DECODE_ADAPTER_xor_reg_off),
    .XOR_ADDRESS(GROUPED_DECODE_ADAPTER_xor_adr), .XOR_ADDRESS_REGISTER(GROUPED_DECODE_ADAPTER_xor_adr_reg),
    .RESULT_VALUE(OPERATIONS_INSTANCE_result_value), .RESULT_IS_VALID(OPERATIONS_INSTANCE_result_is_valid),
    .OVERFLOW(OPERATIONS_INSTANCE_overflow), .INVALID_OPERAND(OPERATIONS_INSTANCE_invalid_operand),
    .DIVIDE_BY_ZERO(OPERATIONS_INSTANCE_divide_by_zero));
  EffectiveAddress EFFECTIVE_ADDRESS_FBOX (
    .DIRECT_ADDR(FETCH_DECODE_opcode[15:0]), .REG_ADDR(ADDRESS_PATH_address),
    .LOAD_ADR_REG(GROUPED_DECODE_ADAPTER_load_adr_reg), .ADD_ADR_REG(GROUPED_DECODE_ADAPTER_add_adr_reg),
    .SUB_ADR_REG(GROUPED_DECODE_ADAPTER_sub_adr_reg), .MUL_ADR_REG(GROUPED_DECODE_ADAPTER_mul_adr_reg),
    .DIV_ADR_REG(GROUPED_DECODE_ADAPTER_div_adr_reg), .AND_ADR_REG(GROUPED_DECODE_ADAPTER_and_adr_reg),
    .OR_ADR_REG(GROUPED_DECODE_ADAPTER_or_adr_reg), .STORE_ADR_REG(GROUPED_DECODE_ADAPTER_store_adr_reg),
    .OFFSET_ADDR(ADDRESS_PATH_address_plus_offset),
    .REG_SELECTED(EFFECTIVE_ADDRESS_FBOX_effective_register_selected_out),
    .LOAD_REG_OFF(GROUPED_DECODE_ADAPTER_load_reg_off), .ADD_REG_OFF(GROUPED_DECODE_ADAPTER_add_reg_off),
    .SUB_REG_OFF(GROUPED_DECODE_ADAPTER_sub_reg_off), .MUL_REG_OFF(GROUPED_DECODE_ADAPTER_mul_reg_off),
    .DIV_REG_OFF(GROUPED_DECODE_ADAPTER_div_reg_off), .AND_REG_OFF(GROUPED_DECODE_ADAPTER_and_reg_off),
    .OR_REG_OFF(GROUPED_DECODE_ADAPTER_or_reg_off), .STORE_REG_OFF(GROUPED_DECODE_ADAPTER_store_reg_off),
    .EFFECTIVE_REGISTER_SELECTED_OUT(EFFECTIVE_ADDRESS_FBOX_effective_register_selected_out),
    .EFFECTIVE_REGISTER_MODE(EFFECTIVE_ADDRESS_FBOX_effective_register_mode),
    .EFFECTIVE_MEMORY_ADDRESS(EFFECTIVE_ADDRESS_FBOX_effective_memory_address),
    .EFFECTIVE_OFFSET_MODE(EFFECTIVE_ADDRESS_FBOX_effective_offset_mode),
    .ADDRESS_OUT_OF_RANGE(EFFECTIVE_ADDRESS_FBOX_address_out_of_range));
  AddressRangeFBox ADDRESS_RANGE_FBOX (
    .OFFSET_CARRY(ADDRESS_PATH_offset_carry),
    .EFFECTIVE_REGISTER_MODE(EFFECTIVE_ADDRESS_FBOX_effective_register_mode),
    .EFFECTIVE_OFFSET_MODE(EFFECTIVE_ADDRESS_FBOX_effective_offset_mode),
    .ADDRESS_OUT_OF_RANGE(EFFECTIVE_ADDRESS_FBOX_address_out_of_range),
    .LOAD_ADDRESS(GROUPED_DECODE_ADAPTER_load_adr), .ADD_ADDRESS(GROUPED_DECODE_ADAPTER_add_adr),
    .SUB_ADDRESS(GROUPED_DECODE_ADAPTER_sub_adr), .MUL_ADDRESS(GROUPED_DECODE_ADAPTER_mul_adr),
    .DIV_ADDRESS(GROUPED_DECODE_ADAPTER_div_adr), .AND_ADDRESS(GROUPED_DECODE_ADAPTER_and_adr),
    .OR_ADDRESS(GROUPED_DECODE_ADAPTER_or_adr), .STORE_ADDRESS(GROUPED_DECODE_ADAPTER_store_adr),
    .ACTIVE_ADDRESS_OUT_OF_RANGE(ADDRESS_RANGE_FBOX_active_address_out_of_range));
  // Probe on ADDRESS_PATH_address_valid
  // Probe on DECODE_SIGNALS_acc_memory_request
  // Probe on DATAPATH_INSTANCE_negative
  // Probe on GROUPED_DECODE_ADAPTER_load_const
  // Probe on OPERATIONS_INSTANCE_overflow
  // Probe on EFFECTIVE_ADDRESS_FBOX_effective_register_selected_out
  // Probe on EFFECTIVE_ADDRESS_FBOX_effective_memory_address
endmodule

module EffectiveAddress (
  input  [15:0] DIRECT_ADDR,
  input  [15:0] REG_ADDR,
  input  LOAD_ADR_REG,
  input  ADD_ADR_REG,
  input  SUB_ADR_REG,
  input  MUL_ADR_REG,
  input  DIV_ADR_REG,
  input  AND_ADR_REG,
  input  OR_ADR_REG,
  input  STORE_ADR_REG,
  input  [15:0] OFFSET_ADDR,
  input  [15:0] REG_SELECTED,
  input  LOAD_REG_OFF,
  input  ADD_REG_OFF,
  input  SUB_REG_OFF,
  input  MUL_REG_OFF,
  input  DIV_REG_OFF,
  input  AND_REG_OFF,
  input  OR_REG_OFF,
  input  STORE_REG_OFF,
  output [15:0] EFFECTIVE_REGISTER_SELECTED_OUT,
  output EFFECTIVE_REGISTER_MODE,
  output [15:0] EFFECTIVE_MEMORY_ADDRESS,
  output EFFECTIVE_OFFSET_MODE,
  output ADDRESS_OUT_OF_RANGE
);

  or MEMORY_ADDRESS_REGISTER_SELECT (EFFECTIVE_REGISTER_MODE, LOAD_ADR_REG, ADD_ADR_REG, SUB_ADR_REG, MUL_ADR_REG, DIV_ADR_REG, AND_ADR_REG, OR_ADR_REG, STORE_ADR_REG);
  or MEMORY_ADDRESS_OFFSET_SELECT (EFFECTIVE_OFFSET_MODE, LOAD_REG_OFF, ADD_REG_OFF, SUB_REG_OFF, MUL_REG_OFF, DIV_REG_OFF, AND_REG_OFF, OR_REG_OFF, STORE_REG_OFF);
  Multiplexer #(.width(16)) multiplexer_1 (
    .in0(DIRECT_ADDR), .in1(REG_ADDR), .out(EFFECTIVE_REGISTER_SELECTED_OUT), .sel(EFFECTIVE_REGISTER_MODE));
  Multiplexer #(.width(16)) multiplexer_2 (
    .in0(OFFSET_ADDR), .in1(REG_SELECTED), .out(EFFECTIVE_MEMORY_ADDRESS), .sel(EFFECTIVE_OFFSET_MODE));
  Comparator #(.width(16)) comparator_1 (
    .a(EFFECTIVE_MEMORY_ADDRESS), .b(16'hfff), .gt(ADDRESS_OUT_OF_RANGE));  // open: eq, lt
endmodule

module Datapath (
  input  [15:0] DATA_IN,
  input  DATAPATH_STARTUP_RESET,
  input  ACC_LOAD,
  input  VALID_IN,
  input  CLK,
  output [15:0] ACC_OUT,
  output ZERO,
  output NEGATIVE,
  output ACC_VALID_OUT
);

  Register #(.width(16)) ACC (.D(DATA_IN), .en(ACC_LOAD), .clk(CLK), .Q(ACC_OUT), .clr(DATAPATH_STARTUP_RESET));
  Register #(.width(1)) ACC_VALID (
    .D(VALID_IN), .en(ACC_LOAD), .clk(CLK), .Q(ACC_VALID_OUT), .clr(DATAPATH_STARTUP_RESET));
  Comparator #(.width(16)) comparator_1 (.a(ACC_OUT), .b({16{1'b0}}), .eq(ZERO), .lt(NEGATIVE));  // open: gt

  // Notes on the sheet:
  //   Clocked 16-bit accumulator; signed comparator derives ZERO and NEGATIVE
endmodule

module AddressPath (
  input  [15:0] ADDRESS_IN,
  input  AR_LOAD,
  input  [15:0] OFFSET,
  input  VALID_IN,
  input  CLK,
  input  ADDRESS_PATH_STARTUP_RESET,
  output [15:0] ADDRESS,
  output [15:0] ADDRESS_PLUS_OFFSET,
  output OFFSET_CARRY,
  output ADDRESS_VALID
);

  Register #(.width(16)) AR (.D(ADDRESS_IN), .en(AR_LOAD), .clk(CLK), .Q(ADDRESS), .clr(ADDRESS_PATH_STARTUP_RESET));
  Register #(.width(1)) AR_VALID (
    .D(VALID_IN), .en(AR_LOAD), .clk(CLK), .Q(ADDRESS_VALID), .clr(ADDRESS_PATH_STARTUP_RESET));
  Adder #(.width(16)) adder_1 (.a(ADDRESS), .b(OFFSET), .out(ADDRESS_PLUS_OFFSET), .cout(OFFSET_CARRY));  // open: cin

  // Notes on the sheet:
  //   Clocked 12-bit address register with combinational offset addition
endmodule

module Memory (
  input  [15:0] ADDRESS,
  input  WRITE_ENABLE,
  input  CLK,
  input  VALID_IN,
  input  [15:0] DATA_IN,
  output MEMORY_VALID,
  output [15:0] MEMORY_DATA
);

  RAM #(.addrWidth(12), .asyncread("true"), .dataWidth(1)) VALID_RAM (
    .addr(ADDRESS[11:0]), .we(WRITE_ENABLE), .oe(1'b1), .clk(CLK), .din(VALID_IN), .dout(MEMORY_VALID));
  RAM #(.addrWidth(12), .asyncread("true"), .dataWidth(16)) DATA_RAM (
    .addr(ADDRESS[11:0]), .we(WRITE_ENABLE), .oe(1'b1), .clk(CLK), .din(DATA_IN), .dout(MEMORY_DATA));

  // Notes on the sheet:
  //   4096-word value/valid memory with shared address, write-enable, and clock
endmodule

module ErrorFlags (
  input  CLEAR_ERROR,
  input  CLK,
  input  SET_OVF,
  input  SET_DIV0,
  input  SET_ADDR,
  input  SET_INV,
  input  SET_ILL,
  input  SET_INPUT,
  output OVF_OUT,
  output DIV0_OUT,
  output ADDR_OUT,
  output INV_OUT,
  output ILL_OUT,
  output INPUT_OUT
);

  wire ERROR_FLAGS_STARTUP_RESET, HOLD_ADDR_out, HOLD_DIV0_out, HOLD_ILL_out, HOLD_INPUT_out, HOLD_INV_out,
       HOLD_OVF_out, NEXT_ADDR_out, NEXT_DIV0_out, NEXT_ILL_out, NEXT_INPUT_out, NEXT_INV_out, NEXT_OVF_out,
       NOT_CLEAR_ERROR_out;

  not NOT_CLEAR_ERROR (NOT_CLEAR_ERROR_out, CLEAR_ERROR);
  and HOLD_OVF (HOLD_OVF_out, OVF_OUT, NOT_CLEAR_ERROR_out);
  and HOLD_DIV0 (HOLD_DIV0_out, DIV0_OUT, NOT_CLEAR_ERROR_out);
  and HOLD_ADDR (HOLD_ADDR_out, ADDR_OUT, NOT_CLEAR_ERROR_out);
  and HOLD_INV (HOLD_INV_out, INV_OUT, NOT_CLEAR_ERROR_out);
  and HOLD_ILL (HOLD_ILL_out, ILL_OUT, NOT_CLEAR_ERROR_out);
  and HOLD_INPUT (HOLD_INPUT_out, INPUT_OUT, NOT_CLEAR_ERROR_out);
  or NEXT_OVF (NEXT_OVF_out, SET_OVF, HOLD_OVF_out);
  or NEXT_DIV0 (NEXT_DIV0_out, SET_DIV0, HOLD_DIV0_out);
  or NEXT_ADDR (NEXT_ADDR_out, SET_ADDR, HOLD_ADDR_out);
  or NEXT_INV (NEXT_INV_out, SET_INV, HOLD_INV_out);
  or NEXT_ILL (NEXT_ILL_out, SET_ILL, HOLD_ILL_out);
  or NEXT_INPUT (NEXT_INPUT_out, SET_INPUT, HOLD_INPUT_out);
  Register #(.width(1)) OVF (.D(NEXT_OVF_out), .en(1'b1), .clk(CLK), .Q(OVF_OUT), .clr(ERROR_FLAGS_STARTUP_RESET));
  Register #(.width(1)) DIV0 (.D(NEXT_DIV0_out), .en(1'b1), .clk(CLK), .Q(DIV0_OUT), .clr(ERROR_FLAGS_STARTUP_RESET));
  Register #(.width(1)) ADDR (.D(NEXT_ADDR_out), .en(1'b1), .clk(CLK), .Q(ADDR_OUT), .clr(ERROR_FLAGS_STARTUP_RESET));
  Register #(.width(1)) INV (.D(NEXT_INV_out), .en(1'b1), .clk(CLK), .Q(INV_OUT), .clr(ERROR_FLAGS_STARTUP_RESET));
  Register #(.width(1)) ILL (.D(NEXT_ILL_out), .en(1'b1), .clk(CLK), .Q(ILL_OUT), .clr(ERROR_FLAGS_STARTUP_RESET));
  Register #(.width(1)) INPUT (
    .D(NEXT_INPUT_out), .en(1'b1), .clk(CLK), .Q(INPUT_OUT), .clr(ERROR_FLAGS_STARTUP_RESET));

  // Notes on the sheet:
  //   Set-dominant sticky flags: SET OR (current AND NOT CLEAR_ERROR)
endmodule

module FetchDecode (
  input  CLK,
  input  RESET,
  input  DEC_JUMP_NOT_ZERO,
  input  NOT_ZERO,
  input  [15:0] PROGRAM_LIMIT,
  input  DEC_HALT_ERROR,
  output JUMP_NOT_ZERO,
  output HALT_ERROR,
  output [11:0] PC_OUT,
  output [21:0] OPCODE
);

  wire PROGRAM_LIMIT_COMPARE_gt;
  wire [15:0] adder_1_out, PC_NEXT_SELECT_out;
  wire [15:12] PC_q;

  Register #(.width(16)) PC (.D(PC_NEXT_SELECT_out), .en(1'b1), .clk(CLK), .Q({PC_q, PC_OUT}), .clr(RESET));
  and JNZ_TAKEN (JUMP_NOT_ZERO, DEC_JUMP_NOT_ZERO, NOT_ZERO);
  Adder #(.width(16)) adder_1 (.a({PC_q, PC_OUT}), .b(16'h1), .out(adder_1_out));  // open: cin, cout
  Comparator #(.width(16)) PROGRAM_LIMIT_COMPARE (
    .a({PC_q, PC_OUT}), .b(PROGRAM_LIMIT), .gt(PROGRAM_LIMIT_COMPARE_gt));  // open: eq, lt
  ROM #(.addrWidth(12), .dataWidth(22)) INSTRUCTION_ROM (.addr(PC_OUT), .data(OPCODE));
  Multiplexer #(.width(16)) PC_NEXT_SELECT (
    .in0(adder_1_out), .in1(OPCODE[15:0]), .out(PC_NEXT_SELECT_out), .sel(JUMP_NOT_ZERO));
  or ERROR_HALT (HALT_ERROR, PROGRAM_LIMIT_COMPARE_gt, DEC_HALT_ERROR);

  // Notes on the sheet:
  //   PROGRAM_LIMIT: initial=0xfff
  //   AP 7 machine format v1: stable six-bit opcode allocation and encoder-generated ROM
  //   contents of INSTRUCTION_ROM (hex, n*v repeats v):
  //   ffff 1c0065 3 1c0064 2a0000 4ffff 1c0064 240004 2c0000
endmodule

module FetchDecodeControls (
  input  [5:0] OPCODE,
  output ADD_OPERAND,
  output SUB_OPERAND,
  output MUL_OPERAND,
  output DIV_OPERAND,
  output AND_OPERAND,
  output OR_OPERAND,
  output XOR_OPERAND,
  output CONST_ARGUMENT,
  output ADDR_ARGUMENT,
  output ADDR_REG_ARGUMENT,
  output ADDR_REG_OFFS_ARGUMENT,
  output NOT,
  output JUMP_ADR,
  output JUMP_ZERO,
  output JUMP_NOT_ZERO,
  output JUMP_NEGATIVE,
  output JUMP_ERROR,
  output JUMP_NOT_ERROR,
  output LOAD_CONST,
  output LOAD_ADR,
  output LOAD_ADR_REG,
  output LOAD_REG_OFF,
  output LD_REG_CONST,
  output LD_REG_ADR,
  output STORE_ADR,
  output STORE_ADR_REG,
  output STORE_REG_OFF,
  output SET_OVF,
  output SET_DIV0,
  output SET_ADDR,
  output SET_INV,
  output SET_ILL,
  output SET_INPUT,
  output CLEAR_ERROR,
  output INPUT,
  output PRINT,
  output PRINT_ADR,
  output HALT,
  output HALT_ERROR,
  output INVALID_OPERAND
);

  wire decoder_1_out0, decoder_1_out1, decoder_1_out2, decoder_1_out3, decoder_1_out4, decoder_1_out5,
       decoder_1_out6, decoder_1_out7, decoder_1_out8, decoder_1_out9, decoder_1_out10, decoder_1_out11,
       decoder_1_out12, decoder_1_out13, decoder_1_out14, decoder_1_out15, decoder_1_out16, decoder_1_out17,
       decoder_1_out18, decoder_1_out19, decoder_1_out20, decoder_1_out21, decoder_1_out22, decoder_1_out23,
       decoder_1_out24, decoder_1_out25, decoder_1_out26, decoder_1_out27, decoder_1_out56, decoder_1_out57,
       decoder_1_out58, decoder_1_out59, decoder_1_out60, decoder_1_out61, decoder_1_out62, decoder_1_out63;

  Decoder #(.select(6)) decoder_1 (
    .out0(decoder_1_out0), .out1(decoder_1_out1), .out2(decoder_1_out2), .out3(decoder_1_out3),
    .out4(decoder_1_out4), .out5(decoder_1_out5), .out6(decoder_1_out6), .out7(decoder_1_out7),
    .out8(decoder_1_out8), .out9(decoder_1_out9), .out10(decoder_1_out10), .out11(decoder_1_out11),
    .out12(decoder_1_out12), .out13(decoder_1_out13), .out14(decoder_1_out14), .out15(decoder_1_out15),
    .out16(decoder_1_out16), .out17(decoder_1_out17), .out18(decoder_1_out18), .out19(decoder_1_out19),
    .out20(decoder_1_out20), .out21(decoder_1_out21), .out22(decoder_1_out22), .out23(decoder_1_out23),
    .out24(decoder_1_out24), .out25(decoder_1_out25), .out26(decoder_1_out26), .out27(decoder_1_out27),
    .out28(NOT), .out29(JUMP_ADR), .out30(JUMP_ZERO), .out31(JUMP_NOT_ZERO), .out32(JUMP_NEGATIVE),
    .out33(JUMP_ERROR), .out34(JUMP_NOT_ERROR), .out35(LOAD_CONST), .out36(LOAD_ADR), .out37(LOAD_ADR_REG),
    .out38(LOAD_REG_OFF), .out39(LD_REG_CONST), .out40(LD_REG_ADR), .out41(STORE_ADR), .out42(STORE_ADR_REG),
    .out43(STORE_REG_OFF), .out44(SET_OVF), .out45(SET_DIV0), .out46(SET_ADDR), .out47(SET_INV),
    .out48(SET_ILL), .out49(SET_INPUT), .out50(CLEAR_ERROR), .out51(INPUT), .out52(PRINT), .out53(PRINT_ADR),
    .out54(HALT), .out55(HALT_ERROR), .out56(decoder_1_out56), .out57(decoder_1_out57),
    .out58(decoder_1_out58), .out59(decoder_1_out59), .out60(decoder_1_out60), .out61(decoder_1_out61),
    .out62(decoder_1_out62), .out63(decoder_1_out63), .sel(OPCODE));  // open: en
  or ADD_OPERAND_SELECT (ADD_OPERAND, decoder_1_out0, decoder_1_out1, decoder_1_out2, decoder_1_out3);
  or SUB_OPERAND_SELECT (SUB_OPERAND, decoder_1_out4, decoder_1_out5, decoder_1_out6, decoder_1_out7);
  or MUL_OPERAND_SELECT (MUL_OPERAND, decoder_1_out8, decoder_1_out9, decoder_1_out10, decoder_1_out11);
  or DIV_OPERAND_SELECT (DIV_OPERAND, decoder_1_out12, decoder_1_out13, decoder_1_out14, decoder_1_out15);
  or AND_OPERAND_SELECT (AND_OPERAND, decoder_1_out16, decoder_1_out17, decoder_1_out18, decoder_1_out19);
  or OR_OPERAND_SELECT (OR_OPERAND, decoder_1_out20, decoder_1_out21, decoder_1_out22, decoder_1_out23);
  or XOR_OPERAND_SELECT (XOR_OPERAND, decoder_1_out24, decoder_1_out25, decoder_1_out26, decoder_1_out27);
  or CONST_ARGUMENT_SELECT (CONST_ARGUMENT, decoder_1_out0, decoder_1_out4, decoder_1_out8, decoder_1_out12, decoder_1_out16, decoder_1_out20, decoder_1_out24);
  or ADDR_ARGUMENT_SELECT (ADDR_ARGUMENT, decoder_1_out1, decoder_1_out5, decoder_1_out9, decoder_1_out13, decoder_1_out17, decoder_1_out21, decoder_1_out25);
  or ADDR_REG_ARGUMENT_SELECT (ADDR_REG_ARGUMENT, decoder_1_out2, decoder_1_out6, decoder_1_out10, decoder_1_out14, decoder_1_out18, decoder_1_out22, decoder_1_out26);
  or ADDR_REG_OFFS_ARGUMENT_SELECT (ADDR_REG_OFFS_ARGUMENT, decoder_1_out3, decoder_1_out7, decoder_1_out11, decoder_1_out15, decoder_1_out19, decoder_1_out23, decoder_1_out27);
  or INVALID_OPERAND_SELECT (INVALID_OPERAND, decoder_1_out56, decoder_1_out57, decoder_1_out58, decoder_1_out59, decoder_1_out60, decoder_1_out61, decoder_1_out62, decoder_1_out63);
endmodule

module IntegrationClock (
  input  CLK,
  output FETCH_CLK,
  output DATAPATH_CLK,
  output ADDRESS_CLK,
  output MEMORY_CLK,
  output ERROR_FLAGS_CLK
);


  assign ADDRESS_CLK = CLK;
  assign DATAPATH_CLK = CLK;
  assign ERROR_FLAGS_CLK = CLK;
  assign FETCH_CLK = CLK;
  assign MEMORY_CLK = CLK;
endmodule

module IntegrationReset (
  input  RESET,
  output FETCH_RESET
);


  assign FETCH_RESET = RESET;
endmodule

module AndArithmeticCircuit (
  input  AND_ACTIVATED,
  input  [15:0] LEFT,
  input  [15:0] RIGHT,
  input  INPUT_VALID,
  output [15:0] RESULT,
  output RESULT_VALID
);

  wire [15:0] BITWISE_AND_out;

  assign BITWISE_AND_out = LEFT & RIGHT;  // AND_Gate BITWISE_AND, 16 bits wide
  Multiplexer #(.width(16)) multiplexer_1 (.in0({16{1'b0}}), .in1(BITWISE_AND_out), .out(RESULT), .sel(AND_ACTIVATED));
  and ACTIVE_AND_VALID (RESULT_VALID, AND_ACTIVATED, INPUT_VALID);

  // Notes on the sheet:
  //   bitwise AND: inactive outputs are neutral
endmodule

module AndSubCircuit (
  input  AND_CONST,
  input  AND_ADDRESS,
  input  AND_ADDRESS_REGISTER,
  input  AND_ADDRESS_REGISTER_PLUS_OFFSET,
  input  [15:0] ACC_VALUE,
  input  [15:0] MEMORY_VALUE,
  input  [15:0] IMMEDIATE_VALUE,
  input  MEMORY_VALID,
  input  ACC_VALID,
  output [15:0] RESULT,
  output RESULT_VALID,
  output RESULT_ACTIVE
);

  wire ACC_AND_VALID_out, multiplexer_2_out;
  wire [15:0] multiplexer_1_out;

  or ACC_AND_MEMORY_SELECT (RESULT_ACTIVE, AND_CONST, AND_ADDRESS, AND_ADDRESS_REGISTER, AND_ADDRESS_REGISTER_PLUS_OFFSET);
  Multiplexer #(.width(16)) multiplexer_1 (
    .in0(MEMORY_VALUE), .in1(IMMEDIATE_VALUE), .out(multiplexer_1_out), .sel(AND_CONST));
  Multiplexer multiplexer_2 (.in0(1'b1), .in1(MEMORY_VALID), .out(multiplexer_2_out), .sel(AND_CONST));
  and ACC_AND_VALID (ACC_AND_VALID_out, multiplexer_2_out, ACC_VALID);
  AndArithmeticCircuit ANDARITHMETICCIRCUIT_1300_440 (
    .AND_ACTIVATED(RESULT_ACTIVE), .LEFT(ACC_VALUE), .RIGHT(multiplexer_1_out),
    .INPUT_VALID(ACC_AND_VALID_out), .RESULT(RESULT), .RESULT_VALID(RESULT_VALID));

  // Notes on the sheet:
  //   MEMORY_VALID →
  //   AND_VALID →
  //   CONST_VALID →
endmodule

module Operations (
  input  ADD_CONST,
  input  ADD_ADDRESS,
  input  ADD_ADDRESS_REGISTER,
  input  ADD_ADDRESS_REGISTER_PLUS_OFFSET,
  input  [15:0] ACC_VALUE,
  input  [15:0] MEMORY_VALUE,
  input  [15:0] IMMEDIATE_VALUE,
  input  MEMORY_VALID,
  input  ACC_VALID,
  input  SUB_CONST,
  input  SUB_ADDRESS,
  input  SUB_ADDRESS_REGISTER,
  input  SUB_ADDRESS_REGISTER_PLUS_OFFSET,
  input  NOT_IS_ACTIVE,
  input  MUL_CONST,
  input  MUL_ADDRESS,
  input  MUL_ADDRESS_REGISTER,
  input  MUL_ADDRESS_REGISTER_PLUS_OFFSET,
  input  DIV_CONST,
  input  DIV_ADDRESS_REGISTER_PLUS_OFFSET,
  input  DIV_ADDRESS,
  input  DIV_ADDRESS_REGISTER,
  input  AND_CONST,
  input  AND_ADDRESS_REGISTER_PLUS_OFFSET,
  input  AND_ADDRESS,
  input  AND_ADDRESS_REGISTER,
  input  OR_CONST,
  input  OR_ADDRESS_REGISTER_PLUS_OFFSET,
  input  OR_ADDRESS,
  input  OR_ADDRESS_REGISTER,
  input  XOR_CONST,
  input  XOR_ADDRESS_REGISTER_PLUS_OFFSET,
  input  XOR_ADDRESS,
  input  XOR_ADDRESS_REGISTER,
  output [15:0] RESULT_VALUE,
  output RESULT_IS_VALID,
  output OVERFLOW,
  output INVALID_OPERAND,
  output DIVIDE_BY_ZERO
);

  wire ADD_OPERATION_overflow, ADD_OPERATION_result_active, ADD_OPERATION_result_valid,
       AND_OPERATION_result_active, AND_OPERATION_result_valid, DIV_OPERATION_result_active,
       DIV_OPERATION_result_valid, MUL_OPERATION_overflow, MUL_OPERATION_result_active,
       MUL_OPERATION_result_valid, not_1_out, NOT_OPERATION_result_active, NOT_OPERATION_result_valid,
       OPERATION_IS_ACTIVE_out, OPERATION_RESULT_VALID_out, OR_OPERATION_result_active,
       OR_OPERATION_result_valid, SUB_OPERATION_overflow, SUB_OPERATION_result_active,
       SUB_OPERATION_result_valid, XOR_OPERATION_result_active, XOR_OPERATION_result_valid;
  wire [15:0] ADD_OPERATION_result, AND_OPERATION_result, DIV_OPERATION_result, MUL_OPERATION_result,
       NOT_OPERATION_result, OR_OPERATION_result, RESULT_out, SUB_OPERATION_result, XOR_OPERATION_result;

  AddSubCircuit ADD_OPERATION (
    .ADD_CONST(ADD_CONST), .ADD_ADDRESS(ADD_ADDRESS), .ADD_ADDRESS_REGISTER(ADD_ADDRESS_REGISTER),
    .ADD_ADDRESS_REGISTER_PLUS_OFFSET(ADD_ADDRESS_REGISTER_PLUS_OFFSET), .ACC_VALUE(ACC_VALUE),
    .MEMORY_VALUE(MEMORY_VALUE), .IMMEDIATE_VALUE(IMMEDIATE_VALUE), .MEMORY_VALID(MEMORY_VALID),
    .ACC_VALID(ACC_VALID), .RESULT(ADD_OPERATION_result), .OVERFLOW(ADD_OPERATION_overflow),
    .RESULT_VALID(ADD_OPERATION_result_valid), .RESULT_ACTIVE(ADD_OPERATION_result_active));
  SubSubCircuit SUB_OPERATION (
    .SUB_CONST(SUB_CONST), .SUB_ADDRESS_REGISTER_PLUS_OFFSET(SUB_ADDRESS),
    .SUB_ADDRESS(SUB_ADDRESS_REGISTER), .SUB_ADDRESS_REGISTER(SUB_ADDRESS_REGISTER_PLUS_OFFSET),
    .ACC_VALUE(ACC_VALUE), .MEMORY_VALUE(MEMORY_VALUE), .IMMEDIATE_VALUE(IMMEDIATE_VALUE),
    .MEMORY_VALID(MEMORY_VALID), .ACC_VALID(ACC_VALID), .RESULT(SUB_OPERATION_result),
    .OVERFLOW(SUB_OPERATION_overflow), .RESULT_VALID(SUB_OPERATION_result_valid),
    .RESULT_ACTIVE(SUB_OPERATION_result_active));
  NotCircuit NOT_OPERATION (
    .ACC_VALUE(ACC_VALUE), .ACC_VALID(ACC_VALID), .NOT_IS_ACTIVE(NOT_IS_ACTIVE),
    .RESULT(NOT_OPERATION_result), .RESULT_VALID(NOT_OPERATION_result_valid),
    .RESULT_ACTIVE(NOT_OPERATION_result_active));
  MulSubCircuit MUL_OPERATION (
    .MUL_CONST(MUL_CONST), .MUL_ADDRESS(MUL_ADDRESS), .MUL_ADDRESS_REGISTER(MUL_ADDRESS_REGISTER),
    .MUL_ADDRESS_REGISTER_PLUS_OFFSET(MUL_ADDRESS_REGISTER_PLUS_OFFSET), .ACC_VALUE(ACC_VALUE),
    .MEMORY_VALUE(MEMORY_VALUE), .IMMEDIATE_VALUE(IMMEDIATE_VALUE), .MEMORY_VALID(MEMORY_VALID),
    .ACC_VALID(ACC_VALID), .RESULT(MUL_OPERATION_result), .OVERFLOW(MUL_OPERATION_overflow),
    .RESULT_VALID(MUL_OPERATION_result_valid), .RESULT_ACTIVE(MUL_OPERATION_result_active));
  DivSubCircuit DIV_OPERATION (
    .DIV_CONST(DIV_CONST), .DIV_ADDRESS(DIV_ADDRESS_REGISTER_PLUS_OFFSET),
    .DIV_ADDRESS_REGISTER(DIV_ADDRESS), .DIV_ADDRESS_REGISTER_PLUS_OFFSET(DIV_ADDRESS_REGISTER),
    .ACC_VALUE(ACC_VALUE), .MEMORY_VALUE(MEMORY_VALUE), .IMMEDIATE_VALUE(IMMEDIATE_VALUE),
    .MEMORY_VALID(MEMORY_VALID), .ACC_VALID(ACC_VALID), .RESULT(DIV_OPERATION_result),
    .RESULT_VALID(DIV_OPERATION_result_valid), .DIVIDE_BY_ZERO(DIVIDE_BY_ZERO),
    .RESULT_ACTIVE(DIV_OPERATION_result_active));
  AndSubCircuit AND_OPERATION (
    .AND_CONST(AND_CONST), .AND_ADDRESS(AND_ADDRESS_REGISTER_PLUS_OFFSET),
    .AND_ADDRESS_REGISTER(AND_ADDRESS), .AND_ADDRESS_REGISTER_PLUS_OFFSET(AND_ADDRESS_REGISTER),
    .ACC_VALUE(ACC_VALUE), .MEMORY_VALUE(MEMORY_VALUE), .IMMEDIATE_VALUE(IMMEDIATE_VALUE),
    .MEMORY_VALID(MEMORY_VALID), .ACC_VALID(ACC_VALID), .RESULT(AND_OPERATION_result),
    .RESULT_VALID(AND_OPERATION_result_valid), .RESULT_ACTIVE(AND_OPERATION_result_active));
  OrSubCircuit OR_OPERATION (
    .OR_CONST(OR_CONST), .OR_ADDRESS(OR_ADDRESS_REGISTER_PLUS_OFFSET), .OR_ADDRESS_REGISTER(OR_ADDRESS),
    .OR_ADDRESS_REGISTER_PLUS_OFFSET(OR_ADDRESS_REGISTER), .ACC_VALUE(ACC_VALUE),
    .MEMORY_VALUE(MEMORY_VALUE), .IMMEDIATE_VALUE(IMMEDIATE_VALUE), .MEMORY_VALID(MEMORY_VALID),
    .ACC_VALID(ACC_VALID), .RESULT(OR_OPERATION_result), .RESULT_VALID(OR_OPERATION_result_valid),
    .RESULT_ACTIVE(OR_OPERATION_result_active));
  XorSubCircuit XOR_OPERATION (
    .XOR_CONST(XOR_CONST), .XOR_ADDRESS(XOR_ADDRESS_REGISTER_PLUS_OFFSET),
    .XOR_ADDRESS_REGISTER(XOR_ADDRESS), .XOR_ADDRESS_REGISTER_PLUS_OFFSET(XOR_ADDRESS_REGISTER),
    .ACC_VALUE(ACC_VALUE), .MEMORY_VALUE(MEMORY_VALUE), .IMMEDIATE_VALUE(IMMEDIATE_VALUE),
    .MEMORY_VALID(MEMORY_VALID), .ACC_VALID(ACC_VALID), .RESULT(XOR_OPERATION_result),
    .RESULT_VALID(XOR_OPERATION_result_valid), .RESULT_ACTIVE(XOR_OPERATION_result_active));
  assign RESULT_out = ADD_OPERATION_result | SUB_OPERATION_result | NOT_OPERATION_result | MUL_OPERATION_result | DIV_OPERATION_result | AND_OPERATION_result | OR_OPERATION_result | XOR_OPERATION_result;  // OR_Gate RESULT, 16 bits wide
  or OPERATION_RESULT_VALID (OPERATION_RESULT_VALID_out, SUB_OPERATION_result_valid, ADD_OPERATION_result_valid, NOT_OPERATION_result_valid, MUL_OPERATION_result_valid, DIV_OPERATION_result_valid, AND_OPERATION_result_valid, OR_OPERATION_result_valid, XOR_OPERATION_result_valid);
  or OVERFLOW_SET (OVERFLOW, SUB_OPERATION_overflow, ADD_OPERATION_overflow, MUL_OPERATION_overflow);
  or OPERATION_IS_ACTIVE (OPERATION_IS_ACTIVE_out, SUB_OPERATION_result_active, ADD_OPERATION_result_active, NOT_OPERATION_result_active, MUL_OPERATION_result_active, DIV_OPERATION_result_active, AND_OPERATION_result_active, OR_OPERATION_result_active, XOR_OPERATION_result_active);
  Multiplexer #(.width(16)) RESULT_DATA_SELECT (
    .in0(IMMEDIATE_VALUE), .in1(RESULT_out), .out(RESULT_VALUE), .sel(OPERATION_IS_ACTIVE_out));
  not not_1 (not_1_out, OPERATION_RESULT_VALID_out);
  Multiplexer multiplexer_1 (
    .in0(1'b1), .in1(OPERATION_RESULT_VALID_out), .out(RESULT_IS_VALID), .sel(OPERATION_IS_ACTIVE_out));
  and ACTIVE_INVALID_OPERATION (INVALID_OPERAND, not_1_out, OPERATION_IS_ACTIVE_out);
endmodule

module NotCircuit (
  input  [15:0] ACC_VALUE,
  input  ACC_VALID,
  input  NOT_IS_ACTIVE,
  output [15:0] RESULT,
  output RESULT_VALID,
  output RESULT_ACTIVE
);

  wire [15:0] NOT_VALUE_out;

  assign NOT_VALUE_out = ~ACC_VALUE;  // NOT_Gate NOT_VALUE, 16 bits wide
  and ACTIVE_NOT_VALID (RESULT_VALID, ACC_VALID, NOT_IS_ACTIVE);
  Multiplexer #(.width(16)) multiplexer_1 (.in0({16{1'b0}}), .in1(NOT_VALUE_out), .out(RESULT), .sel(NOT_IS_ACTIVE));

  assign RESULT_ACTIVE = NOT_IS_ACTIVE;
endmodule

module DecodeSignals (
  input  [5:0] Opcode,
  output ACC_MEMORY_REQUEST,
  output ACC_WRITE_REQUEST
);

  wire ACC_LOAD_REQUEST_out, CONTROL_DECODER_add_operand, CONTROL_DECODER_addr_argument,
       CONTROL_DECODER_addr_reg_argument, CONTROL_DECODER_addr_reg_offs_argument,
       CONTROL_DECODER_and_operand, CONTROL_DECODER_clear_error, CONTROL_DECODER_const_argument,
       CONTROL_DECODER_div_operand, CONTROL_DECODER_halt, CONTROL_DECODER_halt_error, CONTROL_DECODER_input,
       CONTROL_DECODER_invalid_operand, CONTROL_DECODER_jump_adr, CONTROL_DECODER_jump_error,
       CONTROL_DECODER_jump_negative, CONTROL_DECODER_jump_not_error, CONTROL_DECODER_jump_not_zero,
       CONTROL_DECODER_jump_zero, CONTROL_DECODER_ld_reg_adr, CONTROL_DECODER_ld_reg_const,
       CONTROL_DECODER_load_adr, CONTROL_DECODER_load_adr_reg, CONTROL_DECODER_load_const,
       CONTROL_DECODER_load_reg_off, CONTROL_DECODER_mul_operand, CONTROL_DECODER_not,
       CONTROL_DECODER_or_operand, CONTROL_DECODER_print, CONTROL_DECODER_print_adr,
       CONTROL_DECODER_set_addr, CONTROL_DECODER_set_div0, CONTROL_DECODER_set_ill,
       CONTROL_DECODER_set_input, CONTROL_DECODER_set_inv, CONTROL_DECODER_set_ovf,
       CONTROL_DECODER_store_adr, CONTROL_DECODER_store_adr_reg, CONTROL_DECODER_store_reg_off,
       CONTROL_DECODER_sub_operand, CONTROL_DECODER_xor_operand, undriven, undriven_2, undriven_3,
       undriven_4, undriven_5, undriven_6, undriven_7, undriven_8, undriven_9, undriven_10, undriven_11,
       undriven_12, undriven_13, undriven_14, undriven_15, undriven_16;

  FetchDecodeControls CONTROL_DECODER (
    .OPCODE(Opcode), .ADD_OPERAND(CONTROL_DECODER_add_operand), .SUB_OPERAND(CONTROL_DECODER_sub_operand),
    .MUL_OPERAND(CONTROL_DECODER_mul_operand), .DIV_OPERAND(CONTROL_DECODER_div_operand),
    .AND_OPERAND(CONTROL_DECODER_and_operand), .OR_OPERAND(CONTROL_DECODER_or_operand),
    .XOR_OPERAND(CONTROL_DECODER_xor_operand), .CONST_ARGUMENT(CONTROL_DECODER_const_argument),
    .ADDR_ARGUMENT(CONTROL_DECODER_addr_argument), .ADDR_REG_ARGUMENT(CONTROL_DECODER_addr_reg_argument),
    .ADDR_REG_OFFS_ARGUMENT(CONTROL_DECODER_addr_reg_offs_argument), .NOT(CONTROL_DECODER_not),
    .JUMP_ADR(CONTROL_DECODER_jump_adr), .JUMP_ZERO(CONTROL_DECODER_jump_zero),
    .JUMP_NOT_ZERO(CONTROL_DECODER_jump_not_zero), .JUMP_NEGATIVE(CONTROL_DECODER_jump_negative),
    .JUMP_ERROR(CONTROL_DECODER_jump_error), .JUMP_NOT_ERROR(CONTROL_DECODER_jump_not_error),
    .LOAD_CONST(CONTROL_DECODER_load_const), .LOAD_ADR(CONTROL_DECODER_load_adr),
    .LOAD_ADR_REG(CONTROL_DECODER_load_adr_reg), .LOAD_REG_OFF(CONTROL_DECODER_load_reg_off),
    .LD_REG_CONST(CONTROL_DECODER_ld_reg_const), .LD_REG_ADR(CONTROL_DECODER_ld_reg_adr),
    .STORE_ADR(CONTROL_DECODER_store_adr), .STORE_ADR_REG(CONTROL_DECODER_store_adr_reg),
    .STORE_REG_OFF(CONTROL_DECODER_store_reg_off), .SET_OVF(CONTROL_DECODER_set_ovf),
    .SET_DIV0(CONTROL_DECODER_set_div0), .SET_ADDR(CONTROL_DECODER_set_addr),
    .SET_INV(CONTROL_DECODER_set_inv), .SET_ILL(CONTROL_DECODER_set_ill),
    .SET_INPUT(CONTROL_DECODER_set_input), .CLEAR_ERROR(CONTROL_DECODER_clear_error),
    .INPUT(CONTROL_DECODER_input), .PRINT(CONTROL_DECODER_print), .PRINT_ADR(CONTROL_DECODER_print_adr),
    .HALT(CONTROL_DECODER_halt), .HALT_ERROR(CONTROL_DECODER_halt_error),
    .INVALID_OPERAND(CONTROL_DECODER_invalid_operand));
  // Probe on CONTROL_DECODER_jump_not_zero
  // Probe on CONTROL_DECODER_store_adr
  // Probe on CONTROL_DECODER_store_adr_reg
  // Probe on CONTROL_DECODER_store_reg_off
  // Probe on CONTROL_DECODER_set_ovf
  // Probe on CONTROL_DECODER_set_div0
  // Probe on CONTROL_DECODER_set_addr
  // Probe on CONTROL_DECODER_set_inv
  // Probe on CONTROL_DECODER_set_ill
  // Probe on CONTROL_DECODER_set_input
  // Probe on CONTROL_DECODER_input
  // Probe on CONTROL_DECODER_print
  // Probe on CONTROL_DECODER_print_adr
  // Probe on CONTROL_DECODER_halt
  // Probe on CONTROL_DECODER_halt_error
  // Probe on CONTROL_DECODER_invalid_operand
  // Probe on undriven
  // Probe on undriven_2
  // Probe on undriven_3
  // Probe on undriven_4
  // Probe on undriven_5
  // Probe on undriven_6
  // Probe on undriven_7
  // Probe on undriven_8
  // Probe on undriven_9
  // Probe on undriven_10
  // Probe on undriven_11
  // Probe on undriven_12
  // Probe on undriven_13
  // Probe on undriven_14
  // Probe on undriven_15
  or ACC_LOAD_REQUEST (ACC_LOAD_REQUEST_out, CONTROL_DECODER_add_operand, CONTROL_DECODER_sub_operand, CONTROL_DECODER_mul_operand, CONTROL_DECODER_div_operand, CONTROL_DECODER_and_operand, CONTROL_DECODER_or_operand, CONTROL_DECODER_xor_operand, CONTROL_DECODER_const_argument, CONTROL_DECODER_addr_argument, CONTROL_DECODER_addr_reg_argument, CONTROL_DECODER_addr_reg_offs_argument, CONTROL_DECODER_not, CONTROL_DECODER_jump_adr, CONTROL_DECODER_jump_zero, CONTROL_DECODER_jump_negative, CONTROL_DECODER_jump_error, CONTROL_DECODER_jump_not_error, CONTROL_DECODER_load_const, CONTROL_DECODER_load_adr, CONTROL_DECODER_load_adr_reg, CONTROL_DECODER_load_reg_off, CONTROL_DECODER_ld_reg_const, CONTROL_DECODER_ld_reg_adr, CONTROL_DECODER_store_adr, CONTROL_DECODER_store_adr_reg, CONTROL_DECODER_store_reg_off, CONTROL_DECODER_set_ovf);
  or ACC_MEMORY_SELECT (ACC_MEMORY_REQUEST, CONTROL_DECODER_and_operand, CONTROL_DECODER_mul_operand, CONTROL_DECODER_div_operand);
  or ACC_WRITE_AGGREGATOR (ACC_WRITE_REQUEST, ACC_LOAD_REQUEST_out, CONTROL_DECODER_clear_error, undriven_16);
endmodule

module ControlAdapterBlock (
  input  [5:0] OPCODE,
  output LOAD_CONST,
  output LOAD_ADR,
  output LOAD_ADR_REG,
  output LOAD_REG_OFF,
  output ADD_CONST,
  output ADD_ADR,
  output ADD_ADR_REG,
  output ADD_REG_OFF,
  output SUB_CONST,
  output SUB_ADR,
  output SUB_ADR_REG,
  output SUB_REG_OFF,
  output MUL_CONST,
  output MUL_ADR,
  output MUL_ADR_REG,
  output MUL_REG_OFF,
  output DIV_CONST,
  output DIV_ADR,
  output DIV_ADR_REG,
  output DIV_REG_OFF,
  output AND_CONST,
  output AND_ADR,
  output AND_ADR_REG,
  output AND_REG_OFF,
  output OR_CONST,
  output OR_ADR,
  output OR_ADR_REG,
  output OR_REG_OFF,
  output STORE_ADR,
  output STORE_ADR_REG,
  output STORE_REG_OFF,
  output LD_REG_CONST,
  output LD_REG_ADR,
  output NOT,
  output JUMP_ADR,
  output JUMP_ZERO,
  output JUMP_NOT_ZERO,
  output JUMP_NEGATIVE,
  output JUMP_ERROR,
  output JUMP_NOT_ERROR,
  output CLEAR_ERROR,
  output INPUT,
  output PRINT,
  output PRINT_ADR,
  output HALT,
  output HALT_ERROR,
  output SET_OVF,
  output SET_DIV0,
  output SET_ADDR,
  output SET_INV,
  output SET_ILL,
  output SET_INPUT,
  output XOR_CONST,
  output XOR_ADR,
  output XOR_ADR_REG,
  output XOR_REG_OFF
);

  wire decoder_1_out50;

  Decoder #(.select(6)) decoder_1 (
    .out0(LOAD_CONST), .out1(LOAD_ADR), .out2(LOAD_ADR_REG), .out3(LOAD_REG_OFF), .out4(ADD_CONST),
    .out5(ADD_ADR), .out6(ADD_ADR_REG), .out7(ADD_REG_OFF), .out8(SUB_CONST), .out9(SUB_ADR),
    .out10(SUB_ADR_REG), .out11(SUB_REG_OFF), .out12(MUL_CONST), .out13(MUL_ADR), .out14(MUL_ADR_REG),
    .out15(MUL_REG_OFF), .out16(DIV_CONST), .out17(DIV_ADR), .out18(DIV_ADR_REG), .out19(DIV_REG_OFF),
    .out20(AND_CONST), .out21(AND_ADR), .out22(AND_ADR_REG), .out23(AND_REG_OFF), .out24(OR_CONST),
    .out25(OR_ADR), .out26(OR_ADR_REG), .out27(OR_REG_OFF), .out28(STORE_ADR), .out29(STORE_ADR_REG),
    .out30(STORE_REG_OFF), .out31(LD_REG_CONST), .out32(LD_REG_ADR), .out33(NOT), .out34(JUMP_ADR),
    .out35(JUMP_ZERO), .out36(JUMP_NOT_ZERO), .out37(JUMP_NEGATIVE), .out38(JUMP_ERROR),
    .out39(JUMP_NOT_ERROR), .out40(CLEAR_ERROR), .out41(INPUT), .out42(PRINT), .out43(PRINT_ADR),
    .out44(HALT), .out45(HALT_ERROR), .out46(XOR_CONST), .out47(XOR_ADR), .out48(XOR_ADR_REG),
    .out49(XOR_REG_OFF), .out50(decoder_1_out50), .sel(OPCODE));  // open: out51, out52, out53, out54, out55, out56, out57, out58, out59, out60, out61, out62, out63, en

  assign SET_ADDR = 1'b0;
  assign SET_DIV0 = 1'b0;
  assign SET_ILL = 1'b0;
  assign SET_INPUT = 1'b0;
  assign SET_INV = 1'b0;
  assign SET_OVF = 1'b0;
endmodule

module AddSubCircuit (
  input  ADD_CONST,
  input  ADD_ADDRESS,
  input  ADD_ADDRESS_REGISTER,
  input  ADD_ADDRESS_REGISTER_PLUS_OFFSET,
  input  [15:0] ACC_VALUE,
  input  [15:0] MEMORY_VALUE,
  input  [15:0] IMMEDIATE_VALUE,
  input  MEMORY_VALID,
  input  ACC_VALID,
  output [15:0] RESULT,
  output OVERFLOW,
  output RESULT_VALID,
  output RESULT_ACTIVE
);

  wire ACC_ADD_VALID_out, multiplexer_2_out;
  wire [15:0] multiplexer_1_out;

  Multiplexer #(.width(16)) multiplexer_1 (
    .in0(MEMORY_VALUE), .in1(IMMEDIATE_VALUE), .out(multiplexer_1_out), .sel(ADD_CONST));
  Multiplexer multiplexer_2 (.in0(1'b1), .in1(MEMORY_VALID), .out(multiplexer_2_out), .sel(ADD_CONST));
  or ACC_ADD_MEMORY_SELECT (RESULT_ACTIVE, ADD_CONST, ADD_ADDRESS, ADD_ADDRESS_REGISTER, ADD_ADDRESS_REGISTER_PLUS_OFFSET);
  and ACC_ADD_VALID (ACC_ADD_VALID_out, multiplexer_2_out, ACC_VALID);
  AddArithmeticCircuit ADDARITHMETICCIRCUIT_1300_440 (
    .ADD_ACTIVATED(RESULT_ACTIVE), .LEFT(ACC_VALUE), .RIGHT(multiplexer_1_out),
    .INPUT_VALID(ACC_ADD_VALID_out), .RESULT(RESULT), .OVERFLOW(OVERFLOW), .RESULT_VALID(RESULT_VALID));

  // Notes on the sheet:
  //   MEMORY_VALID →
  //   ADD_VALID →
  //   CONST_VALID →
endmodule

module SubSubCircuit (
  input  SUB_CONST,
  input  SUB_ADDRESS_REGISTER_PLUS_OFFSET,
  input  SUB_ADDRESS,
  input  SUB_ADDRESS_REGISTER,
  input  [15:0] ACC_VALUE,
  input  [15:0] MEMORY_VALUE,
  input  [15:0] IMMEDIATE_VALUE,
  input  MEMORY_VALID,
  input  ACC_VALID,
  output [15:0] RESULT,
  output OVERFLOW,
  output RESULT_VALID,
  output RESULT_ACTIVE
);

  wire ACC_SUB_VALID_out, multiplexer_2_out;
  wire [15:0] multiplexer_1_out;

  or ACC_SUB_MEMORY_SELECT (RESULT_ACTIVE, SUB_CONST, SUB_ADDRESS_REGISTER_PLUS_OFFSET, SUB_ADDRESS, SUB_ADDRESS_REGISTER);
  Multiplexer #(.width(16)) multiplexer_1 (
    .in0(MEMORY_VALUE), .in1(IMMEDIATE_VALUE), .out(multiplexer_1_out), .sel(SUB_CONST));
  Multiplexer multiplexer_2 (.in0(1'b1), .in1(MEMORY_VALID), .out(multiplexer_2_out), .sel(SUB_CONST));
  and ACC_SUB_VALID (ACC_SUB_VALID_out, multiplexer_2_out, ACC_VALID);
  SubArithmeticCircuit SUBARITHMETICCIRCUIT_1300_440 (
    .SUB_ACTIVATED(RESULT_ACTIVE), .LEFT(ACC_VALUE), .RIGHT(multiplexer_1_out),
    .INPUT_VALID(ACC_SUB_VALID_out), .RESULT(RESULT), .OVERFLOW(OVERFLOW), .RESULT_VALID(RESULT_VALID));

  // Notes on the sheet:
  //   MEMORY_VALID →
  //   SUB_VALID →
  //   CONST_VALID →
endmodule

module MulSubCircuit (
  input  MUL_CONST,
  input  MUL_ADDRESS,
  input  MUL_ADDRESS_REGISTER,
  input  MUL_ADDRESS_REGISTER_PLUS_OFFSET,
  input  [15:0] ACC_VALUE,
  input  [15:0] MEMORY_VALUE,
  input  [15:0] IMMEDIATE_VALUE,
  input  MEMORY_VALID,
  input  ACC_VALID,
  output [15:0] RESULT,
  output OVERFLOW,
  output RESULT_VALID,
  output RESULT_ACTIVE
);

  wire ACC_MUL_VALID_out, multiplexer_2_out;
  wire [15:0] multiplexer_1_out;

  or ACC_MUL_MEMORY_SELECT (RESULT_ACTIVE, MUL_CONST, MUL_ADDRESS, MUL_ADDRESS_REGISTER, MUL_ADDRESS_REGISTER_PLUS_OFFSET);
  Multiplexer #(.width(16)) multiplexer_1 (
    .in0(MEMORY_VALUE), .in1(IMMEDIATE_VALUE), .out(multiplexer_1_out), .sel(MUL_CONST));
  Multiplexer multiplexer_2 (.in0(1'b1), .in1(MEMORY_VALID), .out(multiplexer_2_out), .sel(MUL_CONST));
  and ACC_MUL_VALID (ACC_MUL_VALID_out, multiplexer_2_out, ACC_VALID);
  MulArithmeticCircuit MULARITHMETICCIRCUIT_1300_440 (
    .MUL_ACTIVATED(RESULT_ACTIVE), .LEFT(ACC_VALUE), .RIGHT(multiplexer_1_out),
    .INPUT_VALID(ACC_MUL_VALID_out), .RESULT(RESULT), .OVERFLOW(OVERFLOW), .RESULT_VALID(RESULT_VALID));

  // Notes on the sheet:
  //   MEMORY_VALID →
  //   MUL_VALID →
  //   CONST_VALID →
endmodule

module MulArithmeticCircuit (
  input  MUL_ACTIVATED,
  input  [15:0] LEFT,
  input  [15:0] RIGHT,
  input  INPUT_VALID,
  output [15:0] RESULT,
  output OVERFLOW,
  output RESULT_VALID
);

  wire NO_OVERFLOW_out, OPERAND_SIGN_DIFFERENT_out, RESULT_SIGN_CHANGED_out;
  wire [14:0] multiplexer_2_out;
  wire [15:0] multiplexer_1_out;
  wire [15:15] multiplexer_2_out_2;

  Multiplexer #(.width(16)) multiplexer_1 (.in0({16{1'b0}}), .in1(LEFT), .out(multiplexer_1_out), .sel(MUL_ACTIVATED));
  Multiplexer #(.width(16)) multiplexer_2 (
    .in0({16{1'b0}}), .in1(RIGHT), .out({multiplexer_2_out_2[15], multiplexer_2_out}), .sel(MUL_ACTIVATED));
  Multiplier #(.width(16)) multiplier_1 (
    .a(multiplexer_1_out), .b({multiplexer_2_out_2[15], multiplexer_2_out}), .out(RESULT));  // open: cin, cout
  xor OPERAND_SIGN_DIFFERENT (OPERAND_SIGN_DIFFERENT_out, multiplexer_1_out[15], multiplexer_2_out_2[15]);
  xor RESULT_SIGN_CHANGED (RESULT_SIGN_CHANGED_out, RESULT[15], multiplexer_1_out[15]);
  not NO_OVERFLOW (NO_OVERFLOW_out, OPERAND_SIGN_DIFFERENT_out);
  and SIGN_OVERFLOW (OVERFLOW, RESULT_SIGN_CHANGED_out, OPERAND_SIGN_DIFFERENT_out);
  and RANGE_VALID (RESULT_VALID, NO_OVERFLOW_out, INPUT_VALID);

  // Notes on the sheet:
  //   signed MUL: overflow = (left_sign XOR right_sign) AND (left_sign XOR result_sign)
endmodule

module DivSubCircuit (
  input  DIV_CONST,
  input  DIV_ADDRESS,
  input  DIV_ADDRESS_REGISTER,
  input  DIV_ADDRESS_REGISTER_PLUS_OFFSET,
  input  [15:0] ACC_VALUE,
  input  [15:0] MEMORY_VALUE,
  input  [15:0] IMMEDIATE_VALUE,
  input  MEMORY_VALID,
  input  ACC_VALID,
  output [15:0] RESULT,
  output RESULT_VALID,
  output DIVIDE_BY_ZERO,
  output RESULT_ACTIVE
);

  wire ACC_DIV_VALID_out, multiplexer_2_out;
  wire [15:0] multiplexer_1_out;

  or ACC_DIV_MEMORY_SELECT (RESULT_ACTIVE, DIV_CONST, DIV_ADDRESS, DIV_ADDRESS_REGISTER, DIV_ADDRESS_REGISTER_PLUS_OFFSET);
  Multiplexer #(.width(16)) multiplexer_1 (
    .in0(MEMORY_VALUE), .in1(IMMEDIATE_VALUE), .out(multiplexer_1_out), .sel(DIV_CONST));
  Multiplexer multiplexer_2 (.in0(1'b1), .in1(MEMORY_VALID), .out(multiplexer_2_out), .sel(DIV_CONST));
  and ACC_DIV_VALID (ACC_DIV_VALID_out, multiplexer_2_out, ACC_VALID);
  DivArithmeticCircuit DIVARITHMETICCIRCUIT_1300_440 (
    .DIV_ACTIVATED(RESULT_ACTIVE), .LEFT(ACC_VALUE), .RIGHT(multiplexer_1_out),
    .INPUT_VALID(ACC_DIV_VALID_out), .RESULT(RESULT), .RESULT_VALID(RESULT_VALID),
    .DIVIDE_BY_ZERO(DIVIDE_BY_ZERO));

  // Notes on the sheet:
  //   MEMORY_VALID →
  //   DIV_VALID →
  //   CONST_VALID →
endmodule

module DivArithmeticCircuit (
  input  DIV_ACTIVATED,
  input  [15:0] LEFT,
  input  [15:0] RIGHT,
  input  INPUT_VALID,
  output [15:0] RESULT,
  output RESULT_VALID,
  output DIVIDE_BY_ZERO
);

  wire NONZERO_DIVISOR_out;
  wire [15:0] multiplexer_1_out, multiplexer_2_out;

  Multiplexer #(.width(16)) multiplexer_1 (.in0({16{1'b0}}), .in1(LEFT), .out(multiplexer_1_out), .sel(DIV_ACTIVATED));
  Multiplexer #(.width(16)) multiplexer_2 (.in0(16'h1), .in1(RIGHT), .out(multiplexer_2_out), .sel(DIV_ACTIVATED));
  Divider #(.width(16)) divider_1 (.a(multiplexer_1_out), .b(multiplexer_2_out), .out(RESULT));  // open: upper, rem
  Comparator #(.width(16)) comparator_1 (.a(multiplexer_2_out), .b(16'h1), .gt(DIVIDE_BY_ZERO));  // open: eq, lt
  not NONZERO_DIVISOR (NONZERO_DIVISOR_out, DIVIDE_BY_ZERO);
  and RANGE_VALID (RESULT_VALID, NONZERO_DIVISOR_out, INPUT_VALID);
endmodule

module AddArithmeticCircuit (
  input  ADD_ACTIVATED,
  input  [15:0] LEFT,
  input  [15:0] RIGHT,
  input  INPUT_VALID,
  output [15:0] RESULT,
  output OVERFLOW,
  output RESULT_VALID
);

  wire NO_OVERFLOW_out, OPERAND_SIGN_DIFFERENT_out, OPERAND_SIGN_SAME_out, RESULT_SIGN_CHANGED_out;
  wire [14:0] multiplexer_2_out;
  wire [15:0] multiplexer_1_out;
  wire [15:15] multiplexer_2_out_2;

  Multiplexer #(.width(16)) multiplexer_1 (.in0({16{1'b0}}), .in1(LEFT), .out(multiplexer_1_out), .sel(ADD_ACTIVATED));
  Multiplexer #(.width(16)) multiplexer_2 (
    .in0({16{1'b0}}), .in1(RIGHT), .out({multiplexer_2_out_2[15], multiplexer_2_out}), .sel(ADD_ACTIVATED));
  Adder #(.width(16)) adder_1 (
    .a(multiplexer_1_out), .b({multiplexer_2_out_2[15], multiplexer_2_out}), .out(RESULT));  // open: cin, cout
  xor OPERAND_SIGN_DIFFERENT (OPERAND_SIGN_DIFFERENT_out, multiplexer_1_out[15], multiplexer_2_out_2[15]);
  not OPERAND_SIGN_SAME (OPERAND_SIGN_SAME_out, OPERAND_SIGN_DIFFERENT_out);
  xor RESULT_SIGN_CHANGED (RESULT_SIGN_CHANGED_out, RESULT[15], multiplexer_1_out[15]);
  not NO_OVERFLOW (NO_OVERFLOW_out, OPERAND_SIGN_SAME_out);
  and SIGN_OVERFLOW (OVERFLOW, RESULT_SIGN_CHANGED_out, OPERAND_SIGN_SAME_out);
  and RANGE_VALID (RESULT_VALID, NO_OVERFLOW_out, INPUT_VALID);

  // Notes on the sheet:
  //   signed ADD: overflow = NOT(left_sign XOR right_sign) AND (left_sign XOR result_sign)
endmodule

module SubArithmeticCircuit (
  input  SUB_ACTIVATED,
  input  [15:0] LEFT,
  input  [15:0] RIGHT,
  input  INPUT_VALID,
  output [15:0] RESULT,
  output OVERFLOW,
  output RESULT_VALID
);

  wire NO_OVERFLOW_out, OPERAND_SIGN_DIFFERENT_out, RESULT_SIGN_CHANGED_out;
  wire [14:0] multiplexer_2_out;
  wire [15:0] multiplexer_1_out;
  wire [15:15] multiplexer_2_out_2;

  Multiplexer #(.width(16)) multiplexer_1 (.in0({16{1'b0}}), .in1(LEFT), .out(multiplexer_1_out), .sel(SUB_ACTIVATED));
  Multiplexer #(.width(16)) multiplexer_2 (
    .in0({16{1'b0}}), .in1(RIGHT), .out({multiplexer_2_out_2[15], multiplexer_2_out}), .sel(SUB_ACTIVATED));
  Subtractor #(.width(16)) subtractor_1 (
    .a(multiplexer_1_out), .b({multiplexer_2_out_2[15], multiplexer_2_out}), .out(RESULT));  // open: bin, bout
  xor OPERAND_SIGN_DIFFERENT (OPERAND_SIGN_DIFFERENT_out, multiplexer_1_out[15], multiplexer_2_out_2[15]);
  xor RESULT_SIGN_CHANGED (RESULT_SIGN_CHANGED_out, RESULT[15], multiplexer_1_out[15]);
  not NO_OVERFLOW (NO_OVERFLOW_out, OPERAND_SIGN_DIFFERENT_out);
  and SIGN_OVERFLOW (OVERFLOW, RESULT_SIGN_CHANGED_out, OPERAND_SIGN_DIFFERENT_out);
  and RANGE_VALID (RESULT_VALID, NO_OVERFLOW_out, INPUT_VALID);

  // Notes on the sheet:
  //   signed SUB: overflow = (left_sign XOR right_sign) AND (left_sign XOR result_sign)
endmodule

module AddressRangeFBox (
  input  OFFSET_CARRY,
  input  EFFECTIVE_REGISTER_MODE,
  input  EFFECTIVE_OFFSET_MODE,
  input  ADDRESS_OUT_OF_RANGE,
  input  LOAD_ADDRESS,
  input  ADD_ADDRESS,
  input  SUB_ADDRESS,
  input  MUL_ADDRESS,
  input  DIV_ADDRESS,
  input  AND_ADDRESS,
  input  OR_ADDRESS,
  input  STORE_ADDRESS,
  output ACTIVE_ADDRESS_OUT_OF_RANGE
);

  wire ACTIVE_ADDRESS_RANGE_GATE_out, ACTIVE_OFFSET_ADDRESS_ERROR_out, DIRECT_MEMORY_ADDRESS_ACTIVE_out,
       MEMORY_ADDRESS_ACTIVE_out;

  or DIRECT_MEMORY_ADDRESS_ACTIVE (DIRECT_MEMORY_ADDRESS_ACTIVE_out, LOAD_ADDRESS, ADD_ADDRESS, SUB_ADDRESS, MUL_ADDRESS, DIV_ADDRESS, AND_ADDRESS, OR_ADDRESS, STORE_ADDRESS);
  or MEMORY_ADDRESS_ACTIVE (MEMORY_ADDRESS_ACTIVE_out, DIRECT_MEMORY_ADDRESS_ACTIVE_out, EFFECTIVE_REGISTER_MODE, EFFECTIVE_OFFSET_MODE);
  and ACTIVE_ADDRESS_RANGE_GATE (ACTIVE_ADDRESS_RANGE_GATE_out, MEMORY_ADDRESS_ACTIVE_out, ADDRESS_OUT_OF_RANGE);
  and ACTIVE_OFFSET_ADDRESS_ERROR (ACTIVE_OFFSET_ADDRESS_ERROR_out, OFFSET_CARRY, EFFECTIVE_OFFSET_MODE);
  or ACTIVE_ADDRESS_ERROR (ACTIVE_ADDRESS_OUT_OF_RANGE, ACTIVE_OFFSET_ADDRESS_ERROR_out, ACTIVE_ADDRESS_RANGE_GATE_out);
endmodule

module OrArithmeticCircuit (
  input  OR_ACTIVATED,
  input  [15:0] LEFT,
  input  [15:0] RIGHT,
  input  INPUT_VALID,
  output [15:0] RESULT,
  output RESULT_VALID
);

  wire [15:0] BITWISE_OR_out;

  assign BITWISE_OR_out = LEFT | RIGHT;  // OR_Gate BITWISE_OR, 16 bits wide
  Multiplexer #(.width(16)) multiplexer_1 (.in0({16{1'b0}}), .in1(BITWISE_OR_out), .out(RESULT), .sel(OR_ACTIVATED));
  and ACTIVE_OR_VALID (RESULT_VALID, OR_ACTIVATED, INPUT_VALID);

  // Notes on the sheet:
  //   bitwise OR: inactive outputs are neutral
endmodule

module OrSubCircuit (
  input  OR_CONST,
  input  OR_ADDRESS,
  input  OR_ADDRESS_REGISTER,
  input  OR_ADDRESS_REGISTER_PLUS_OFFSET,
  input  [15:0] ACC_VALUE,
  input  [15:0] MEMORY_VALUE,
  input  [15:0] IMMEDIATE_VALUE,
  input  MEMORY_VALID,
  input  ACC_VALID,
  output [15:0] RESULT,
  output RESULT_VALID,
  output RESULT_ACTIVE
);

  wire ACC_OR_VALID_out, multiplexer_2_out;
  wire [15:0] multiplexer_1_out;

  or ACC_OR_MEMORY_SELECT (RESULT_ACTIVE, OR_CONST, OR_ADDRESS, OR_ADDRESS_REGISTER, OR_ADDRESS_REGISTER_PLUS_OFFSET);
  Multiplexer #(.width(16)) multiplexer_1 (
    .in0(MEMORY_VALUE), .in1(IMMEDIATE_VALUE), .out(multiplexer_1_out), .sel(OR_CONST));
  Multiplexer multiplexer_2 (.in0(1'b1), .in1(MEMORY_VALID), .out(multiplexer_2_out), .sel(OR_CONST));
  and ACC_OR_VALID (ACC_OR_VALID_out, multiplexer_2_out, ACC_VALID);
  OrArithmeticCircuit ORARITHMETICCIRCUIT_1300_440 (
    .OR_ACTIVATED(RESULT_ACTIVE), .LEFT(ACC_VALUE), .RIGHT(multiplexer_1_out),
    .INPUT_VALID(ACC_OR_VALID_out), .RESULT(RESULT), .RESULT_VALID(RESULT_VALID));

  // Notes on the sheet:
  //   MEMORY_VALID →
  //   OR_VALID →
  //   CONST_VALID →
endmodule

module XorArithmeticCircuit (
  input  XOR_ACTIVATED,
  input  [15:0] LEFT,
  input  [15:0] RIGHT,
  input  INPUT_VALID,
  output [15:0] RESULT,
  output RESULT_VALID
);

  wire [15:0] BITWISE_XOR_out;

  assign BITWISE_XOR_out = LEFT ^ RIGHT;  // XOR_Gate BITWISE_XOR, 16 bits wide
  Multiplexer #(.width(16)) multiplexer_1 (.in0({16{1'b0}}), .in1(BITWISE_XOR_out), .out(RESULT), .sel(XOR_ACTIVATED));
  and ACTIVE_XOR_VALID (RESULT_VALID, XOR_ACTIVATED, INPUT_VALID);

  // Notes on the sheet:
  //   bitwise XOR: inactive outputs are neutral
endmodule

module XorSubCircuit (
  input  XOR_CONST,
  input  XOR_ADDRESS,
  input  XOR_ADDRESS_REGISTER,
  input  XOR_ADDRESS_REGISTER_PLUS_OFFSET,
  input  [15:0] ACC_VALUE,
  input  [15:0] MEMORY_VALUE,
  input  [15:0] IMMEDIATE_VALUE,
  input  MEMORY_VALID,
  input  ACC_VALID,
  output [15:0] RESULT,
  output RESULT_VALID,
  output RESULT_ACTIVE
);

  wire ACC_XOR_VALID_out, multiplexer_2_out;
  wire [15:0] multiplexer_1_out;

  or ACC_XOR_MEMORY_SELECT (RESULT_ACTIVE, XOR_CONST, XOR_ADDRESS, XOR_ADDRESS_REGISTER, XOR_ADDRESS_REGISTER_PLUS_OFFSET);
  Multiplexer #(.width(16)) multiplexer_1 (
    .in0(MEMORY_VALUE), .in1(IMMEDIATE_VALUE), .out(multiplexer_1_out), .sel(XOR_CONST));
  Multiplexer multiplexer_2 (.in0(1'b1), .in1(MEMORY_VALID), .out(multiplexer_2_out), .sel(XOR_CONST));
  and ACC_XOR_VALID (ACC_XOR_VALID_out, multiplexer_2_out, ACC_VALID);
  XorArithmeticCircuit ORARITHMETICCIRCUIT_1300_440 (
    .XOR_ACTIVATED(RESULT_ACTIVE), .LEFT(ACC_VALUE), .RIGHT(multiplexer_1_out),
    .INPUT_VALID(ACC_XOR_VALID_out), .RESULT(RESULT), .RESULT_VALID(RESULT_VALID));

  // Notes on the sheet:
  //   MEMORY_VALID →
  //   XOR_VALID →
  //   CONST_VALID →
endmodule
