// Logisim project TinyCPU_Peripherals.circ as structural Verilog: 5 circuits, main circuit TinyCPUSystemMain
module TinyCPUSystemMain (
  input  CLK,
  input  RESET,
  input  INTERRUPT_REQUEST,
  output [15:0] OUTPUT_PORT_VALUE,
  output OUTPUT_PORT_VALID,
  output INTERRUPT_PENDING,
  output INTERRUPT_ENABLED,
  output [11:0] RETURN_ADDRESS,
  output RETURN_ADDRESS_VALID,
  output IN_INTERRUPT_HANDLER
);

  wire cpuintegrationboundary_1_disable_request, cpuintegrationboundary_1_enable_request,
       cpuintegrationboundary_1_instruction_boundary, cpuintegrationboundary_1_return_request,
       cpuintegrationboundary_1_write_enable, cpuintegrationboundary_1_write_valid,
       interruptcontroller_1_illegal_return, interruptcontroller_1_interrupt_accept,
       outputmemorypath_1_ram_write_enable, outputmemorypath_1_read_valid;
  wire [11:0] cpuintegrationboundary_1_address, cpuintegrationboundary_1_next_pc,
       interruptcontroller_1_target_pc;
  wire [15:0] cpuintegrationboundary_1_write_value, outputmemorypath_1_read_value;

  OutputMemoryPath outputmemorypath_1 (
    .ADDRESS(cpuintegrationboundary_1_address), .WRITE_VALUE(cpuintegrationboundary_1_write_value),
    .WRITE_VALID(cpuintegrationboundary_1_write_enable), .WRITE_ENABLE(cpuintegrationboundary_1_write_valid),
    .CLK(CLK), .RESET(RESET), .READ_VALUE(outputmemorypath_1_read_value),
    .READ_VALID(outputmemorypath_1_read_valid), .OUTPUT_PORT_VALUE(OUTPUT_PORT_VALUE),
    .OUTPUT_PORT_VALID(OUTPUT_PORT_VALID), .RAM_WRITE_ENABLE(outputmemorypath_1_ram_write_enable));  // open: RAM_READ_VALUE, RAM_READ_VALID
  InterruptController interruptcontroller_1 (
    .RESET(RESET), .CLK(CLK), .INTERRUPT_REQUEST(INTERRUPT_REQUEST),
    .INSTRUCTION_BOUNDARY(cpuintegrationboundary_1_instruction_boundary),
    .ENABLE_REQUEST(cpuintegrationboundary_1_enable_request),
    .DISABLE_REQUEST(cpuintegrationboundary_1_disable_request),
    .RETURN_REQUEST(cpuintegrationboundary_1_return_request), .NEXT_PC(cpuintegrationboundary_1_next_pc),
    .INTERRUPT_ACCEPT(interruptcontroller_1_interrupt_accept), .INTERRUPT_PENDING(INTERRUPT_PENDING),
    .INTERRUPT_ENABLED(INTERRUPT_ENABLED), .ILLEGAL_RETURN(interruptcontroller_1_illegal_return),
    .RETURN_ADDRESS(RETURN_ADDRESS), .TARGET_PC(interruptcontroller_1_target_pc),
    .RETURN_ADDRESS_VALID(RETURN_ADDRESS_VALID), .IN_INTERRUPT_HANDLER(IN_INTERRUPT_HANDLER));
  CPUIntegrationBoundary cpuintegrationboundary_1 (
    .RAM_READ_VALUE(outputmemorypath_1_read_value), .RAM_READ_VALID(outputmemorypath_1_read_valid),
    .RAM_WRITE_ENABLE(outputmemorypath_1_ram_write_enable),
    .INTERRUPT_ACCEPT(interruptcontroller_1_interrupt_accept),
    .ILLEGAL_RETURN(interruptcontroller_1_illegal_return), .TARGET_PC(interruptcontroller_1_target_pc),
    .ADDRESS(cpuintegrationboundary_1_address), .WRITE_VALUE(cpuintegrationboundary_1_write_value),
    .WRITE_ENABLE(cpuintegrationboundary_1_write_enable), .WRITE_VALID(cpuintegrationboundary_1_write_valid),
    .INSTRUCTION_BOUNDARY(cpuintegrationboundary_1_instruction_boundary),
    .ENABLE_REQUEST(cpuintegrationboundary_1_enable_request),
    .DISABLE_REQUEST(cpuintegrationboundary_1_disable_request),
    .RETURN_REQUEST(cpuintegrationboundary_1_return_request), .NEXT_PC(cpuintegrationboundary_1_next_pc));  // open: CLK, RESET, CORE_ADDRESS, CORE_WRITE_VALUE, CORE_WRITE_ENABLE, CORE_WRITE_VALID, CORE_INSTRUCTION_BOUNDARY, CORE_ENABLE_REQUEST, CORE_DISABLE_REQUEST, CORE_RETURN_REQUEST, CORE_NEXT_PC, READ_VALUE, READ_VALID
endmodule

module CPUIntegrationBoundary (
  input  CLK,
  input  RESET,
  input  [15:0] RAM_READ_VALUE,
  input  RAM_READ_VALID,
  input  [11:0] CORE_ADDRESS,
  input  [15:0] CORE_WRITE_VALUE,
  input  RAM_WRITE_ENABLE,
  input  CORE_WRITE_ENABLE,
  input  CORE_WRITE_VALID,
  input  CORE_INSTRUCTION_BOUNDARY,
  input  CORE_ENABLE_REQUEST,
  input  CORE_DISABLE_REQUEST,
  input  INTERRUPT_ACCEPT,
  input  CORE_RETURN_REQUEST,
  input  [11:0] CORE_NEXT_PC,
  input  ILLEGAL_RETURN,
  input  [11:0] TARGET_PC,
  output [15:0] READ_VALUE,
  output READ_VALID,
  output [11:0] ADDRESS,
  output [15:0] WRITE_VALUE,
  output WRITE_ENABLE,
  output WRITE_VALID,
  output INSTRUCTION_BOUNDARY,
  output ENABLE_REQUEST,
  output DISABLE_REQUEST,
  output RETURN_REQUEST,
  output [11:0] NEXT_PC
);

  TinyCPUMain tinycpumain_1 (
    .CLK(CLK), .RESET(RESET), .EXTERNAL_MEMORY_VALUE(RAM_READ_VALUE), .EXTERNAL_MEMORY_VALID(RAM_READ_VALID),
    .USE_EXTERNAL_MEMORY(1'b1));  // open: PRINT_VALUE, PRINT_ADDRESS_VALUE, PRINT_ADDRESS_VALID, EXTERNAL_WRITE_VALUE, EXTERNAL_WRITE_VALID, EXTERNAL_WRITE_ENABLE, INSTRUCTION_BOUNDARY, ENABLE_INTERRUPTS_REQUEST, DISABLE_INTERRUPTS_REQUEST, RETURN_FROM_INTERRUPT_REQUEST, ERROR_OVF, ERROR_DIV0, ERROR_ADDR, ERROR_INV, ERROR_ILL, ERROR_INPUT, NEXT_PC, PRINT_ENABLE, PRINT_ADDRESS_ENABLE, HALTED, HALTED_WITH_ERROR

  assign ADDRESS = CORE_ADDRESS;
  assign DISABLE_REQUEST = CORE_DISABLE_REQUEST;
  assign ENABLE_REQUEST = CORE_ENABLE_REQUEST;
  assign INSTRUCTION_BOUNDARY = CORE_INSTRUCTION_BOUNDARY;
  assign NEXT_PC = CORE_NEXT_PC;
  assign RETURN_REQUEST = CORE_RETURN_REQUEST;
  assign WRITE_ENABLE = CORE_WRITE_ENABLE;
  assign WRITE_VALID = CORE_WRITE_VALID;
  assign WRITE_VALUE = CORE_WRITE_VALUE;
endmodule

module OutputPort (
  input  [15:0] WRITE_VALUE,
  input  WRITE_VALID,
  input  WRITE_ENABLE,
  input  CLK,
  input  RESET,
  output [15:0] VALUE,
  output VALID
);

  wire OUTPUT_WRITE_ACCEPTED_out;

  and OUTPUT_WRITE_ACCEPTED (OUTPUT_WRITE_ACCEPTED_out, WRITE_VALID, WRITE_ENABLE);
  Register #(.width(16)) OUTPUT_VALUE (
    .D(WRITE_VALUE), .en(OUTPUT_WRITE_ACCEPTED_out), .clk(CLK), .Q(VALUE), .clr(RESET));
  Register #(.width(1)) OUTPUT_VALID (
    .D(WRITE_VALID), .en(OUTPUT_WRITE_ACCEPTED_out), .clk(CLK), .Q(VALID), .clr(RESET));
endmodule

module OutputMemoryPath (
  input  [15:0] RAM_READ_VALUE,
  input  RAM_READ_VALID,
  input  [11:0] ADDRESS,
  input  [15:0] WRITE_VALUE,
  input  WRITE_VALID,
  input  WRITE_ENABLE,
  input  CLK,
  input  RESET,
  output [15:0] READ_VALUE,
  output READ_VALID,
  output [15:0] OUTPUT_PORT_VALUE,
  output OUTPUT_PORT_VALID,
  output RAM_WRITE_ENABLE
);

  wire comparator_1_eq, OUTPUT_WRITE_GATE_out;

  Comparator #(.width(12)) comparator_1 (.a(ADDRESS), .b({12{1'b1}}), .eq(comparator_1_eq));  // open: gt, lt
  and OUTPUT_WRITE_GATE (OUTPUT_WRITE_GATE_out, WRITE_VALID, comparator_1_eq, WRITE_ENABLE);
  and RAM_WRITE_GATE (RAM_WRITE_ENABLE, ~comparator_1_eq, WRITE_ENABLE);  // AND_Gate
  Register #(.width(16)) OUTPUT_VALUE (
    .D(WRITE_VALUE), .en(OUTPUT_WRITE_GATE_out), .clk(CLK), .Q(OUTPUT_PORT_VALUE), .clr(RESET));
  Register #(.width(1)) OUTPUT_VALID (
    .D(WRITE_VALID), .en(OUTPUT_WRITE_GATE_out), .clk(CLK), .Q(OUTPUT_PORT_VALID), .clr(RESET));
  Multiplexer #(.width(16)) multiplexer_1 (
    .in0(RAM_READ_VALUE), .in1(OUTPUT_PORT_VALUE), .out(READ_VALUE), .sel(comparator_1_eq));
  Multiplexer multiplexer_2 (.in0(RAM_READ_VALID), .in1(OUTPUT_PORT_VALID), .out(READ_VALID), .sel(comparator_1_eq));

  // Notes on the sheet:
  //   OUTPUT MEMORY PATH — address 0xFFF selects output port
endmodule

module InterruptController (
  input  RESET,
  input  CLK,
  input  INTERRUPT_REQUEST,
  input  INSTRUCTION_BOUNDARY,
  input  ENABLE_REQUEST,
  input  DISABLE_REQUEST,
  input  RETURN_REQUEST,
  input  [11:0] NEXT_PC,
  output INTERRUPT_ACCEPT,
  output INTERRUPT_PENDING,
  output INTERRUPT_ENABLED,
  output ILLEGAL_RETURN,
  output [11:0] RETURN_ADDRESS,
  output [11:0] TARGET_PC,
  output RETURN_ADDRESS_VALID,
  output IN_INTERRUPT_HANDLER
);

  wire HANDLER_HOLD_out, HANDLER_NEXT_out, MASK_HOLD_out, MASK_NEXT_out, PENDING_HOLD_UNTIL_ACCEPT_out,
       PENDING_SET_OR_HOLD_out, REQUEST_LEVEL_q, RETURN_VALID_HOLD_out, RETURN_VALID_NEXT_out,
       RISING_EDGE_DETECT_out, VALID_RETURN_GATE_out;

  and RISING_EDGE_DETECT (RISING_EDGE_DETECT_out, ~REQUEST_LEVEL_q, INTERRUPT_REQUEST);  // AND_Gate
  and PENDING_HOLD_UNTIL_ACCEPT (PENDING_HOLD_UNTIL_ACCEPT_out, INTERRUPT_PENDING, ~INTERRUPT_ACCEPT);  // AND_Gate
  and MASK_HOLD (MASK_HOLD_out, INTERRUPT_ENABLED, ~DISABLE_REQUEST, ~INTERRUPT_ACCEPT);  // AND_Gate
  and RETURN_VALID_HOLD (RETURN_VALID_HOLD_out, RETURN_ADDRESS_VALID, ~VALID_RETURN_GATE_out);  // AND_Gate
  and HANDLER_HOLD (HANDLER_HOLD_out, IN_INTERRUPT_HANDLER, ~VALID_RETURN_GATE_out);  // AND_Gate
  or PENDING_SET_OR_HOLD (PENDING_SET_OR_HOLD_out, RISING_EDGE_DETECT_out, PENDING_HOLD_UNTIL_ACCEPT_out);
  or MASK_NEXT (MASK_NEXT_out, ENABLE_REQUEST, VALID_RETURN_GATE_out, MASK_HOLD_out);
  or RETURN_VALID_NEXT (RETURN_VALID_NEXT_out, INTERRUPT_ACCEPT, RETURN_VALID_HOLD_out);
  or HANDLER_NEXT (HANDLER_NEXT_out, INTERRUPT_ACCEPT, HANDLER_HOLD_out);
  Register #(.width(1)) REQUEST_LEVEL (.D(INTERRUPT_REQUEST), .en(1'b1), .clk(CLK), .Q(REQUEST_LEVEL_q), .clr(RESET));
  Register #(.width(1)) register_1 (
    .D(PENDING_SET_OR_HOLD_out), .en(1'b1), .clk(CLK), .Q(INTERRUPT_PENDING), .clr(RESET));
  Register #(.width(1)) register_2 (.D(MASK_NEXT_out), .en(1'b1), .clk(CLK), .Q(INTERRUPT_ENABLED), .clr(RESET));
  Register #(.width(12)) register_3 (.D(NEXT_PC), .en(INTERRUPT_ACCEPT), .clk(CLK), .Q(RETURN_ADDRESS), .clr(RESET));
  Register #(.width(1)) register_4 (
    .D(RETURN_VALID_NEXT_out), .en(1'b1), .clk(CLK), .Q(RETURN_ADDRESS_VALID), .clr(RESET));
  Register #(.width(1)) register_5 (.D(HANDLER_NEXT_out), .en(1'b1), .clk(CLK), .Q(IN_INTERRUPT_HANDLER), .clr(RESET));
  and INTERRUPT_ACCEPT_GATE (INTERRUPT_ACCEPT, INSTRUCTION_BOUNDARY, INTERRUPT_PENDING, INTERRUPT_ENABLED, ~IN_INTERRUPT_HANDLER);  // AND_Gate
  and VALID_RETURN_GATE (VALID_RETURN_GATE_out, RETURN_REQUEST, RETURN_ADDRESS_VALID, IN_INTERRUPT_HANDLER);
  and ILLEGAL_RETURN_GATE (ILLEGAL_RETURN, RETURN_REQUEST, ~VALID_RETURN_GATE_out);  // AND_Gate
  Multiplexer #(.width(12)) multiplexer_1 (
    .in0(12'hff0), .in1(RETURN_ADDRESS), .out(TARGET_PC), .sel(VALID_RETURN_GATE_out));

  // Notes on the sheet:
  //   EDGE / INPUTS
  //   NEXT-STATE LOGIC
  //   feedback buses: ACCEPT / VALID_RETURN
  //   STATE REGISTERS
  //   ACCEPT / RETURN DECODE
endmodule
