// Logisim project TinyCPU-AddArithmeticCircuit.circ as structural Verilog: 1 circuit, main circuit AddArithmeticCircuit
module AddArithmeticCircuit (
  input  ADD_ACTIVATED,
  input  [15:0] LEFT,
  input  [15:0] RIGHT,
  input  INPUT_VALID,
  output [15:0] RESULT,
  output OVERFLOW,
  output RESULT_VALID
);

  wire NO_OVERFLOW_out, OPERAND_SIGN_DIFFERENT_out, OPERAND_SIGN_SAME_out, RESULT_SIGN_CHANGED_out;
  wire [14:0] multiplexer_2_out;
  wire [15:0] multiplexer_1_out;
  wire [15:15] multiplexer_2_out_2;

  Multiplexer #(.width(16)) multiplexer_1 (.in0({16{1'b0}}), .in1(LEFT), .out(multiplexer_1_out), .sel(ADD_ACTIVATED));
  Multiplexer #(.width(16)) multiplexer_2 (
    .in0({16{1'b0}}), .in1(RIGHT), .out({multiplexer_2_out_2[15], multiplexer_2_out}), .sel(ADD_ACTIVATED));
  Adder #(.width(16)) adder_1 (
    .a(multiplexer_1_out), .b({multiplexer_2_out_2[15], multiplexer_2_out}), .out(RESULT));  // open: cin, cout
  xor OPERAND_SIGN_DIFFERENT (OPERAND_SIGN_DIFFERENT_out, multiplexer_1_out[15], multiplexer_2_out_2[15]);
  not OPERAND_SIGN_SAME (OPERAND_SIGN_SAME_out, OPERAND_SIGN_DIFFERENT_out);
  xor RESULT_SIGN_CHANGED (RESULT_SIGN_CHANGED_out, RESULT[15], multiplexer_1_out[15]);
  not NO_OVERFLOW (NO_OVERFLOW_out, OPERAND_SIGN_SAME_out);
  and SIGN_OVERFLOW (OVERFLOW, RESULT_SIGN_CHANGED_out, OPERAND_SIGN_SAME_out);
  and RANGE_VALID (RESULT_VALID, NO_OVERFLOW_out, INPUT_VALID);

  // Notes on the sheet:
  //   signed ADD: overflow = NOT(left_sign XOR
  //   right_sign) AND (left_sign XOR result_sign)
  //   OPERAND SIGN DIFFERENT
  //   OPERAND SIGN SAME
  //   RESULT SIGN CHANGED
  //   NO OVERFLOW
  //   SIGN OVERFLOW
  //   RANGE VALID
endmodule
