// Logisim project TinyCPU-AddressRangeFBox.circ as structural Verilog: 1 circuit, main circuit AddressRangeFBox
module AddressRangeFBox (
  input  OFFSET_CARRY,
  input  EFFECTIVE_REGISTER_MODE,
  input  EFFECTIVE_OFFSET_MODE,
  input  ADDRESS_OUT_OF_RANGE,
  input  LOAD_ADDRESS,
  input  ADD_ADDRESS,
  input  SUB_ADDRESS,
  input  MUL_ADDRESS,
  input  DIV_ADDRESS,
  input  AND_ADDRESS,
  input  OR_ADDRESS,
  input  STORE_ADDRESS,
  output ACTIVE_ADDRESS_OUT_OF_RANGE
);

  wire ACTIVE_ADDRESS_RANGE_GATE_out, ACTIVE_OFFSET_ADDRESS_ERROR_out, DIRECT_MEMORY_ADDRESS_ACTIVE_out,
       MEMORY_ADDRESS_ACTIVE_out;

  or DIRECT_MEMORY_ADDRESS_ACTIVE (DIRECT_MEMORY_ADDRESS_ACTIVE_out, LOAD_ADDRESS, ADD_ADDRESS, SUB_ADDRESS, MUL_ADDRESS, DIV_ADDRESS, AND_ADDRESS, OR_ADDRESS, STORE_ADDRESS);
  or MEMORY_ADDRESS_ACTIVE (MEMORY_ADDRESS_ACTIVE_out, DIRECT_MEMORY_ADDRESS_ACTIVE_out, EFFECTIVE_REGISTER_MODE, EFFECTIVE_OFFSET_MODE);
  and ACTIVE_ADDRESS_RANGE_GATE (ACTIVE_ADDRESS_RANGE_GATE_out, MEMORY_ADDRESS_ACTIVE_out, ADDRESS_OUT_OF_RANGE);
  and ACTIVE_OFFSET_ADDRESS_ERROR (ACTIVE_OFFSET_ADDRESS_ERROR_out, OFFSET_CARRY, EFFECTIVE_OFFSET_MODE);
  or ACTIVE_ADDRESS_ERROR (ACTIVE_ADDRESS_OUT_OF_RANGE, ACTIVE_OFFSET_ADDRESS_ERROR_out, ACTIVE_ADDRESS_RANGE_GATE_out);

  // Notes on the sheet:
  //   DIRECT MEMORY ADDRESS ACTIVE
  //   MEMORY ADDRESS ACTIVE
  //   ACTIVE ADDRESS RANGE GATE
  //   ACTIVE OFFSET ADDRESS ERROR
  //   ACTIVE ADDRESS ERROR
endmodule
