// Logisim project TinyCPU-AndArithmeticCircuit.circ as structural Verilog: 1 circuit, main circuit AndArithmeticCircuit
module AndArithmeticCircuit (
  input  AND_ACTIVATED,
  input  [15:0] LEFT,
  input  [15:0] RIGHT,
  input  INPUT_VALID,
  output [15:0] RESULT,
  output RESULT_VALID
);

  wire [15:0] BITWISE_AND_out;

  assign BITWISE_AND_out = LEFT & RIGHT;  // AND_Gate BITWISE_AND, 16 bits wide
  Multiplexer #(.width(16)) multiplexer_1 (.in0({16{1'b0}}), .in1(BITWISE_AND_out), .out(RESULT), .sel(AND_ACTIVATED));
  and ACTIVE_AND_VALID (RESULT_VALID, AND_ACTIVATED, INPUT_VALID);

  // Notes on the sheet:
  //   BITWISE AND
  //   bitwise AND: inactive outputs
  //   are neutral
  //   ACTIVE AND VALID
endmodule
