// Logisim project TinyCPU-DivArithmeticCircuit.circ as structural Verilog: 1 circuit, main circuit DivArithmeticCircuit
module DivArithmeticCircuit (
  input  DIV_ACTIVATED,
  input  [15:0] LEFT,
  input  [15:0] RIGHT,
  input  INPUT_VALID,
  output [15:0] RESULT,
  output RESULT_VALID,
  output DIVIDE_BY_ZERO
);

  wire NONZERO_DIVISOR_out;
  wire [15:0] multiplexer_1_out, multiplexer_2_out;

  Multiplexer #(.width(16)) multiplexer_1 (.in0({16{1'b0}}), .in1(LEFT), .out(multiplexer_1_out), .sel(DIV_ACTIVATED));
  Multiplexer #(.width(16)) multiplexer_2 (.in0(16'h1), .in1(RIGHT), .out(multiplexer_2_out), .sel(DIV_ACTIVATED));
  Divider #(.mode("twosComplement"), .width(16)) divider_1 (
    .a(multiplexer_1_out), .b(multiplexer_2_out), .out(RESULT));  // open: upper, rem
  Comparator #(.width(16)) comparator_1 (.a(multiplexer_2_out), .b(16'h1), .gt(DIVIDE_BY_ZERO));  // open: eq, lt
  not NONZERO_DIVISOR (NONZERO_DIVISOR_out, DIVIDE_BY_ZERO);
  and RANGE_VALID (RESULT_VALID, NONZERO_DIVISOR_out, INPUT_VALID);
endmodule
