// Logisim project TinyCPU-EffectiveAddress.circ as structural Verilog: 1 circuit, main circuit EffectiveAddress
module EffectiveAddress (
  input  [15:0] DIRECT_ADDR,
  input  [15:0] REG_ADDR,
  input  LOAD_ADR_REG,
  input  ADD_ADR_REG,
  input  SUB_ADR_REG,
  input  MUL_ADR_REG,
  input  DIV_ADR_REG,
  input  AND_ADR_REG,
  input  OR_ADR_REG,
  input  STORE_ADR_REG,
  input  [15:0] OFFSET_ADDR,
  input  [15:0] REG_SELECTED,
  input  LOAD_REG_OFF,
  input  ADD_REG_OFF,
  input  SUB_REG_OFF,
  input  MUL_REG_OFF,
  input  DIV_REG_OFF,
  input  AND_REG_OFF,
  input  OR_REG_OFF,
  input  STORE_REG_OFF,
  output [15:0] EFFECTIVE_REGISTER_SELECTED_OUT,
  output EFFECTIVE_REGISTER_MODE,
  output [15:0] EFFECTIVE_MEMORY_ADDRESS,
  output EFFECTIVE_OFFSET_MODE,
  output ADDRESS_OUT_OF_RANGE
);

  or MEMORY_ADDRESS_REGISTER_SELECT (EFFECTIVE_REGISTER_MODE, LOAD_ADR_REG, ADD_ADR_REG, SUB_ADR_REG, MUL_ADR_REG, DIV_ADR_REG, AND_ADR_REG, OR_ADR_REG, STORE_ADR_REG);
  or MEMORY_ADDRESS_OFFSET_SELECT (EFFECTIVE_OFFSET_MODE, LOAD_REG_OFF, ADD_REG_OFF, SUB_REG_OFF, MUL_REG_OFF, DIV_REG_OFF, AND_REG_OFF, OR_REG_OFF, STORE_REG_OFF);
  Multiplexer #(.width(16)) multiplexer_1 (
    .in0(DIRECT_ADDR), .in1(REG_ADDR), .out(EFFECTIVE_REGISTER_SELECTED_OUT), .sel(EFFECTIVE_REGISTER_MODE));
  Multiplexer #(.width(16)) multiplexer_2 (
    .in0(OFFSET_ADDR), .in1(REG_SELECTED), .out(EFFECTIVE_MEMORY_ADDRESS), .sel(EFFECTIVE_OFFSET_MODE));
  Comparator #(.width(16)) comparator_1 (
    .a(EFFECTIVE_MEMORY_ADDRESS), .b(16'hfff), .gt(ADDRESS_OUT_OF_RANGE));  // open: eq, lt

  // Notes on the sheet:
  //   MEMORY ADDRESS REGISTER SELECT
  //   MEMORY ADDRESS OFFSET SELECT
endmodule
