// Logisim project TinyCPU-FetchDecode.circ as structural Verilog: 1 circuit, main circuit FetchDecode
module FetchDecode (
  input  CLK,
  input  RESET,
  input  DEC_JUMP_NOT_ZERO,
  input  NOT_ZERO,
  input  [11:0] PROGRAM_LIMIT,
  input  DEC_HALT_ERROR,
  input  INTERRUPT_ACCEPT,
  input  [11:0] INTERRUPT_TARGET_PC,
  output JUMP_NOT_ZERO_OCCURED,
  output HALT_ERROR,
  output [11:0] PC_OUT,
  output [21:0] OPCODE
);

  wire comparator_1_gt;
  wire [11:0] adder_1_out, INTERRUPT_PC_OVERRIDE_out, multiplexer_1_out;

  Register #(.width(12)) PC (.D(INTERRUPT_PC_OVERRIDE_out), .en(1'b1), .clk(CLK), .Q(PC_OUT), .clr(RESET));
  and JNZ_TAKEN (JUMP_NOT_ZERO_OCCURED, DEC_JUMP_NOT_ZERO, NOT_ZERO);
  Adder #(.width(12)) adder_1 (.a(PC_OUT), .b(12'h1), .out(adder_1_out));  // open: cin, cout
  Comparator #(.width(12)) comparator_1 (.a(PC_OUT), .b(PROGRAM_LIMIT), .gt(comparator_1_gt));  // open: eq, lt
  Multiplexer #(.width(12)) multiplexer_1 (
    .in0(adder_1_out), .in1(OPCODE[11:0]), .out(multiplexer_1_out), .sel(JUMP_NOT_ZERO_OCCURED));
  ROM #(.addrWidth(12), .dataWidth(22)) INSTRUCTION_ROM (.addr(PC_OUT), .data(OPCODE));
  Multiplexer #(.width(12)) INTERRUPT_PC_OVERRIDE (
    .in0(multiplexer_1_out), .in1(INTERRUPT_TARGET_PC), .out(INTERRUPT_PC_OVERRIDE_out),
    .sel(INTERRUPT_ACCEPT));
  or ERROR_HALT (HALT_ERROR, comparator_1_gt, DEC_HALT_ERROR);

  // Notes on the sheet:
  //   PROGRAM_LIMIT: initial=0xfff
  //   AP 7 machine format v1: stable six-bit opcode allocation and encoder-generated ROM
  //   contents of INSTRUCTION_ROM (hex, n*v repeats v):
  //   23ffff 290065 230003 290064 340000 ffff 290064 1f0004 360000
endmodule
