// Logisim project TinyCPU-FetchDecodeControls.circ as structural Verilog: 1 circuit, main circuit FetchDecodeControls
module FetchDecodeControls (
  input  [5:0] OPCODE,
  output ADD_OPERAND,
  output SUB_OPERAND,
  output MUL_OPERAND,
  output DIV_OPERAND,
  output AND_OPERAND,
  output OR_OPERAND,
  output XOR_OPERAND,
  output LOAD_OPERAND,
  output STORE_OPERAND,
  output CONST_ARGUMENT,
  output ADDR_ARGUMENT,
  output ADDR_REG_ARGUMENT,
  output ADDR_REG_OFFS_ARGUMENT,
  output NOT,
  output JUMP_ADR,
  output JUMP_ZERO,
  output JUMP_NOT_ZERO,
  output JUMP_NEGATIVE,
  output JUMP_ERROR,
  output JUMP_NOT_ERROR,
  output SET_OVF,
  output SET_DIV0,
  output SET_ADDR,
  output SET_INV,
  output SET_ILL,
  output SET_INPUT,
  output CLEAR_ERROR,
  output INPUT,
  output PRINT,
  output PRINT_ADR,
  output HALT,
  output HALT_ERROR,
  output INVALID_OPERAND
);

  wire decoder_1_out0, decoder_1_out1, decoder_1_out2, decoder_1_out3, decoder_1_out4, decoder_1_out5,
       decoder_1_out6, decoder_1_out7, decoder_1_out8, decoder_1_out9, decoder_1_out10, decoder_1_out11,
       decoder_1_out12, decoder_1_out13, decoder_1_out14, decoder_1_out15, decoder_1_out16, decoder_1_out17,
       decoder_1_out18, decoder_1_out19, decoder_1_out20, decoder_1_out21, decoder_1_out22, decoder_1_out23,
       decoder_1_out24, decoder_1_out25, decoder_1_out26, decoder_1_out27, decoder_1_out28, decoder_1_out29,
       decoder_1_out30, decoder_1_out31, decoder_1_out32, decoder_1_out46, decoder_1_out47, decoder_1_out48,
       decoder_1_out49, decoder_1_out50, decoder_1_out51, decoder_1_out52, decoder_1_out53, decoder_1_out54,
       decoder_1_out55, decoder_1_out56, decoder_1_out57, decoder_1_out58, decoder_1_out59, decoder_1_out60,
       decoder_1_out61, decoder_1_out62, decoder_1_out63, undriven, undriven_2, undriven_3, undriven_4,
       undriven_5, undriven_6, undriven_7, undriven_8, undriven_9, undriven_10, undriven_11, undriven_12,
       undriven_13, undriven_14, undriven_15, undriven_16, undriven_17, undriven_18, undriven_19,
       undriven_20, undriven_21, undriven_22, undriven_23, undriven_24, undriven_25, undriven_26,
       undriven_27, undriven_28, undriven_29, undriven_30, undriven_31, undriven_32, undriven_33,
       undriven_34, undriven_35, undriven_36;

  Decoder #(.select(6)) decoder_1 (
    .out0(decoder_1_out0), .out1(decoder_1_out1), .out2(decoder_1_out2), .out3(decoder_1_out3),
    .out4(decoder_1_out4), .out5(decoder_1_out5), .out6(decoder_1_out6), .out7(decoder_1_out7),
    .out8(decoder_1_out8), .out9(decoder_1_out9), .out10(decoder_1_out10), .out11(decoder_1_out11),
    .out12(decoder_1_out12), .out13(decoder_1_out13), .out14(decoder_1_out14), .out15(decoder_1_out15),
    .out16(decoder_1_out16), .out17(decoder_1_out17), .out18(decoder_1_out18), .out19(decoder_1_out19),
    .out20(decoder_1_out20), .out21(decoder_1_out21), .out22(decoder_1_out22), .out23(decoder_1_out23),
    .out24(decoder_1_out24), .out25(decoder_1_out25), .out26(decoder_1_out26), .out27(decoder_1_out27),
    .out28(decoder_1_out28), .out29(decoder_1_out29), .out30(decoder_1_out30), .out31(decoder_1_out31),
    .out32(decoder_1_out32), .out33(NOT), .out34(JUMP_ADR), .out35(JUMP_ZERO), .out36(JUMP_NOT_ZERO),
    .out37(JUMP_NEGATIVE), .out38(JUMP_ERROR), .out39(JUMP_NOT_ERROR), .out40(CLEAR_ERROR), .out41(INPUT),
    .out42(PRINT), .out43(PRINT_ADR), .out44(HALT), .out45(HALT_ERROR), .out46(decoder_1_out46),
    .out47(decoder_1_out47), .out48(decoder_1_out48), .out49(decoder_1_out49), .out50(decoder_1_out50),
    .out51(decoder_1_out51), .out52(decoder_1_out52), .out53(decoder_1_out53), .out54(decoder_1_out54),
    .out55(decoder_1_out55), .out56(decoder_1_out56), .out57(decoder_1_out57), .out58(decoder_1_out58),
    .out59(decoder_1_out59), .out60(decoder_1_out60), .out61(decoder_1_out61), .out62(decoder_1_out62),
    .out63(decoder_1_out63), .sel(OPCODE));  // open: en
  or ADD_OPERAND_SELECT (ADD_OPERAND, undriven_32, undriven_33, undriven_35, undriven_36);
  or SUB_OPERAND_SELECT (SUB_OPERAND, undriven, undriven_2, undriven_3, undriven_4);
  or MUL_OPERAND_SELECT (MUL_OPERAND, undriven_5, undriven_6, undriven_7, undriven_8);
  or DIV_OPERAND_SELECT (DIV_OPERAND, undriven_9, undriven_10, undriven_11, undriven_12);
  or AND_OPERAND_SELECT (AND_OPERAND, undriven_13, undriven_14, undriven_15, undriven_16);
  or OR_OPERAND_SELECT (OR_OPERAND, undriven_17, undriven_18, undriven_19, undriven_20);
  or XOR_OPERAND_SELECT (XOR_OPERAND, undriven_21, undriven_22, undriven_23, undriven_24);
  or LOAD_OPERAND_SELECT (LOAD_OPERAND, undriven_25, undriven_26, undriven_27, undriven_28);
  or STORE_OPERAND_SELECT (STORE_OPERAND, undriven_29, undriven_30, undriven_31);
  or CONST_ARGUMENT_SELECT (CONST_ARGUMENT, decoder_1_out0, undriven_32, decoder_1_out8, decoder_1_out12, decoder_1_out16, decoder_1_out20, decoder_1_out24, decoder_1_out31, decoder_1_out46);
  or ADDR_ARGUMENT_SELECT (ADDR_ARGUMENT, decoder_1_out1, undriven_33, decoder_1_out9, decoder_1_out13, decoder_1_out17, decoder_1_out21, decoder_1_out25, decoder_1_out28, decoder_1_out32, undriven_34, decoder_1_out47);
  or ADDR_REG_ARGUMENT_SELECT (ADDR_REG_ARGUMENT, decoder_1_out2, undriven_35, decoder_1_out10, decoder_1_out14, decoder_1_out18, decoder_1_out22, decoder_1_out26, decoder_1_out29, decoder_1_out48);
  or ADDR_REG_OFFS_ARGUMENT_SELECT (ADDR_REG_OFFS_ARGUMENT, decoder_1_out3, undriven_36, decoder_1_out11, decoder_1_out15, decoder_1_out19, decoder_1_out23, decoder_1_out27, decoder_1_out30, decoder_1_out49);
  or INVALID_OPERAND_SELECT (INVALID_OPERAND, decoder_1_out50, decoder_1_out51, decoder_1_out52, decoder_1_out53, decoder_1_out54, decoder_1_out55, decoder_1_out56, decoder_1_out57, decoder_1_out58, decoder_1_out59, decoder_1_out60, decoder_1_out61, decoder_1_out62, decoder_1_out63);

  assign SET_ADDR = 1'b0;
  assign SET_DIV0 = 1'b0;
  assign SET_ILL = 1'b0;
  assign SET_INPUT = 1'b0;
  assign SET_INV = 1'b0;
  assign SET_OVF = 1'b0;

  // Notes on the sheet:
  //   Ein gemeinsamer 6-zu-64-Decoder versorgt alle Steuersignale.
  //   ODER-Gatter gruppieren Operation und Argumentart; keine Decoderduplikate.
  //   ADD_OPERAND: Decoder-Ausgang
  //   SUB_OPERAND: Decoder-Ausgang
  //   MUL_OPERAND: Decoder-Ausgang
  //   DIV_OPERAND: Decoder-Ausgang
  //   AND_OPERAND: Decoder-Ausgang
  //   OR_OPERAND: Decoder-Ausgang
  //   XOR_OPERAND: Decoder-Ausgang
  //   LOAD_OPERAND: Decoder-Ausgang
  //   STORE_OPERAND: Decoder-Ausgang
  //   CONST_ARGUMENT: Decoder-Ausgang
  //   ADDR_ARGUMENT: Decoder-Ausgang
  //   ADDR_REG_ARGUMENT: Decoder-Ausgang
  //   ADDR_REG_OFFS_ARGUMENT: Decoder-Ausgang
  //   NOT: Decoder-Ausgang
  //   JUMP_ADR: Decoder-Ausgang
  //   JUMP_ZERO: Decoder-Ausgang
  //   JUMP_NOT_ZERO: Decoder-Ausgang
  //   JUMP_NEGATIVE: Decoder-Ausgang
  //   JUMP_ERROR: Decoder-Ausgang
  //   JUMP_NOT_ERROR: Decoder-Ausgang
  //   SET_OVF: Decoder-Ausgang
  //   SET_DIV0: Decoder-Ausgang
  //   SET_ADDR: Decoder-Ausgang
  //   SET_INV: Decoder-Ausgang
  //   SET_ILL: Decoder-Ausgang
  //   SET_INPUT: Decoder-Ausgang
  //   CLEAR_ERROR: Decoder-Ausgang
  //   INPUT: Decoder-Ausgang
  //   PRINT: Decoder-Ausgang
  //   PRINT_ADR: Decoder-Ausgang
  //   HALT: Decoder-Ausgang
  //   HALT_ERROR: Decoder-Ausgang
  //   INVALID_OPERAND: Decoder-Ausgang
endmodule
