// Logisim project TinyCPU-Memory.circ as structural Verilog: 1 circuit, main circuit Memory
module Memory (
  input  [15:0] ADDRESS,
  input  WRITE_ENABLE,
  input  CLK,
  input  VALID_IN,
  input  [15:0] DATA_IN,
  output MEMORY_VALID,
  output [15:0] MEMORY_DATA
);

  RAM #(.addrWidth(12), .asyncread("true"), .dataWidth(1)) VALID_RAM (
    .addr(ADDRESS[11:0]), .we(WRITE_ENABLE), .oe(1'b1), .clk(CLK), .din(VALID_IN), .dout(MEMORY_VALID));
  RAM #(.addrWidth(12), .asyncread("true"), .dataWidth(16)) DATA_RAM (
    .addr(ADDRESS[11:0]), .we(WRITE_ENABLE), .oe(1'b1), .clk(CLK), .din(DATA_IN), .dout(MEMORY_DATA));

  // Notes on the sheet:
  //   4096-word value/valid memory with shared
  //   address, write-enable, and clock
endmodule
