// Logisim project TinyCPU-MulArithmeticCircuit.circ as structural Verilog: 1 circuit, main circuit MulArithmeticCircuit
module MulArithmeticCircuit (
  input  MUL_ACTIVATED,
  input  [15:0] LEFT,
  input  [15:0] RIGHT,
  input  INPUT_VALID,
  output [15:0] RESULT,
  output OVERFLOW,
  output RESULT_VALID
);

  wire comparator_1_eq, PRODUCT_OUT_OF_RANGE_out;
  wire [15:0] multiplexer_1_out, multiplexer_2_out, multiplexer_3_out, multiplier_1_cout;

  Multiplexer #(.width(16)) multiplexer_1 (.in0({16{1'b0}}), .in1(LEFT), .out(multiplexer_1_out), .sel(MUL_ACTIVATED));
  Multiplexer #(.width(16)) multiplexer_2 (.in0({16{1'b0}}), .in1(RIGHT), .out(multiplexer_2_out), .sel(MUL_ACTIVATED));
  Multiplier #(.width(16), .mode("twosComplement")) multiplier_1 (
    .a(multiplexer_1_out), .b(multiplexer_2_out), .out(RESULT), .cin({16{1'b0}}), .cout(multiplier_1_cout));
  Multiplexer #(.width(16)) multiplexer_3 (
    .in0({16{1'b0}}), .in1({16{1'b1}}), .out(multiplexer_3_out), .sel(RESULT[15]));
  Comparator #(.width(16), .mode("unsigned")) comparator_1 (
    .a(multiplier_1_cout), .b(multiplexer_3_out), .eq(comparator_1_eq));  // open: gt, lt
  not PRODUCT_OUT_OF_RANGE (PRODUCT_OUT_OF_RANGE_out, comparator_1_eq);
  and SIGN_OVERFLOW (OVERFLOW, PRODUCT_OUT_OF_RANGE_out, MUL_ACTIVATED, INPUT_VALID);
  and RANGE_VALID (RESULT_VALID, comparator_1_eq, MUL_ACTIVATED, INPUT_VALID);

  // Notes on the sheet:
  //   Vorzeichenbehaftete Multiplikation: volle 32-Bit-Bereichspruefung
  //   Erwartetes Oberwort
  //   Oberwort vergleichen
  //   Ueberlauf
  //   Gueltiges Ergebnis
endmodule
