// Logisim project TinyCPU-NotCircuit.circ as structural Verilog: 1 circuit, main circuit NotCircuit
module NotCircuit (
  input  [15:0] ACC_VALUE,
  input  ACC_VALID,
  input  NOT_IS_ACTIVE,
  output [15:0] RESULT,
  output RESULT_VALID,
  output RESULT_ACTIVE
);

  wire [15:0] NOT_VALUE_out;

  assign NOT_VALUE_out = ~ACC_VALUE;  // NOT_Gate NOT_VALUE, 16 bits wide
  and ACTIVE_NOT_VALID (RESULT_VALID, ACC_VALID, NOT_IS_ACTIVE);
  Multiplexer #(.width(16)) multiplexer_1 (.in0({16{1'b0}}), .in1(NOT_VALUE_out), .out(RESULT), .sel(NOT_IS_ACTIVE));

  assign RESULT_ACTIVE = NOT_IS_ACTIVE;

  // Notes on the sheet:
  //   NOT VALUE
  //   ACTIVE NOT VALID
endmodule
