// Logisim project TinyCPU-OrArithmeticCircuit.circ as structural Verilog: 1 circuit, main circuit OrArithmeticCircuit
module OrArithmeticCircuit (
  input  OR_ACTIVATED,
  input  [15:0] LEFT,
  input  [15:0] RIGHT,
  input  INPUT_VALID,
  output [15:0] RESULT,
  output RESULT_VALID
);

  wire [15:0] BITWISE_OR_out;

  assign BITWISE_OR_out = LEFT | RIGHT;  // OR_Gate BITWISE_OR, 16 bits wide
  Multiplexer #(.width(16)) multiplexer_1 (.in0({16{1'b0}}), .in1(BITWISE_OR_out), .out(RESULT), .sel(OR_ACTIVATED));
  and ACTIVE_OR_VALID (RESULT_VALID, OR_ACTIVATED, INPUT_VALID);

  // Notes on the sheet:
  //   BITWISE OR
  //   bitwise OR: inactive outputs
  //   are neutral
  //   ACTIVE OR VALID
endmodule
