// Logisim project TinyCPU-XorArithmeticCircuit.circ as structural Verilog: 1 circuit, main circuit XorArithmeticCircuit
module XorArithmeticCircuit (
  input  XOR_ACTIVATED,
  input  [15:0] LEFT,
  input  [15:0] RIGHT,
  input  INPUT_VALID,
  output [15:0] RESULT,
  output RESULT_VALID
);

  wire [15:0] BITWISE_XOR_out;

  assign BITWISE_XOR_out = LEFT ^ RIGHT;  // XOR_Gate BITWISE_XOR, 16 bits wide
  Multiplexer #(.width(16)) multiplexer_1 (.in0({16{1'b0}}), .in1(BITWISE_XOR_out), .out(RESULT), .sel(XOR_ACTIVATED));
  and ACTIVE_XOR_VALID (RESULT_VALID, XOR_ACTIVATED, INPUT_VALID);

  // Notes on the sheet:
  //   BITWISE XOR
  //   bitwise XOR: inactive outputs
  //   are neutral
  //   ACTIVE XOR VALID
endmodule
